// Logisim project 1.circ as structural Verilog: 1 circuit, main circuit main
module main (
  input  in_1,
  input  in_2,
  input  in_3,
  input  in_4,
  output out_5,
  output out_6
);

  NotExactlyOne xnor_1 (.out(out_5), .in0(in_1), .in1(in_2), .in2(in_3), .in3(in_4));
  xnor even_parity_1 (out_6, in_1, in_2, in_3, in_4);
endmodule
