// Logisim project cpu.circ as structural Verilog
module memory (
  input  [15:0] AD_IN,
  input  [15:0] VALUE_IN,
  input  IRWrite,
  input  MemWrite,
  input  clock,
  input  MemRead,
  output [15:0] IR,
  output [15:0] DR
);

  wire not_1_out;
  wire [15:0] ram_1_data;

  not not_1 (not_1_out, clock);
  RAM #(.addrWidth(16), .dataWidth(16), .bus("separate")) ram_1 (
    .addr(AD_IN), .din(VALUE_IN), .data(ram_1_data), .str(MemWrite), .clk(not_1_out), .ld(MemRead));  // open: sel, clr
  Register #(.width(16), .trigger("high")) u_IR (.D(ram_1_data), .en(MemRead), .Q(IR), .clk(IRWrite));  // open: clr
  Register #(.width(16), .trigger("high")) register_1 (
    .D(ram_1_data), .en(MemRead), .Q(DR), .clk(MemRead));  // open: clr
endmodule

module registerSet (
  input  [15:0] link_WR,
  input  [1:0] selectRA,
  input  [1:0] selectR,
  input  RegWrite,
  input  [1:0] selectRB,
  output [15:0] out1,
  output [15:0] out2,
  output [15:0] reg3,
  output [15:0] reg0,
  output [15:0] reg2,
  output [15:0] reg1
);

  wire and_1_out, and_2_out, and_3_out, and_4_out, decoder_1_out0, decoder_1_out1, decoder_1_out2,
       decoder_1_out3, not_1_out, not_2_out;

  Decoder #(.select(2), .enable("false")) decoder_1 (
    .out0(decoder_1_out0), .out1(decoder_1_out1), .out2(decoder_1_out2), .out3(decoder_1_out3), .sel(selectR));
  and and_1 (and_1_out, decoder_1_out0, RegWrite);
  and and_2 (and_2_out, decoder_1_out1, RegWrite);
  and and_3 (and_3_out, decoder_1_out2, RegWrite);
  and and_4 (and_4_out, decoder_1_out3, RegWrite);
  not not_1 (not_1_out, RegWrite);
  not not_2 (not_2_out, RegWrite);
  Register #(.width(16), .trigger("falling")) register_1 (
    .D(link_WR), .en(and_1_out), .Q(reg0), .clk(not_1_out));  // open: clr
  Register #(.width(16), .trigger("falling")) register_2 (
    .D(link_WR), .en(and_2_out), .Q(reg1), .clk(not_1_out));  // open: clr
  Register #(.width(16), .trigger("falling")) register_3 (
    .D(link_WR), .en(and_3_out), .Q(reg2), .clk(not_1_out));  // open: clr
  Register #(.width(16), .trigger("falling")) register_4 (
    .D(link_WR), .en(and_4_out), .Q(reg3), .clk(not_2_out));  // open: clr
  Multiplexer #(.select(2), .width(16), .enable("false")) multiplexer_1 (
    .in0(reg0), .in1(reg1), .in2(reg2), .in3(reg3), .out(out1), .sel(selectRA));
  Multiplexer #(.select(2), .width(16), .enable("false")) multiplexer_2 (
    .in0(reg0), .in1(reg1), .in2(reg2), .in3(reg3), .out(out2), .sel(selectRB));
endmodule

module ALU (
  input  [15:0] IN1,
  input  [15:0] IN2,
  input  [1:0] FUNCTION,
  input  jFunctoin,
  output [15:0] OUTPUT,
  output ZERO
);

  wire nor_1_out;
  wire [15:0] adder_1_out, and_1_out, or_1_out, subtractor_1_out;

  Adder #(.width(16)) adder_1 (.a(IN1), .b(IN2), .out(adder_1_out));  // open: cin, cout
  Subtractor #(.width(16)) subtractor_1 (.a(IN1), .b(IN2), .out(subtractor_1_out));  // open: bin, bout
  assign and_1_out = IN1 & IN2;  // AND_Gate and_1, 16 bits wide
  assign or_1_out = IN1 | IN2;  // OR_Gate or_1, 16 bits wide
  Multiplexer #(.select(2), .width(16), .enable("false")) multiplexer_1 (
    .in0(adder_1_out), .in1(subtractor_1_out), .in2(and_1_out), .in3(or_1_out), .out(OUTPUT), .sel(FUNCTION));
  nor nor_1 (nor_1_out, OUTPUT[0], OUTPUT[1], OUTPUT[2], OUTPUT[3], OUTPUT[4], OUTPUT[5], OUTPUT[6], OUTPUT[7], OUTPUT[9], OUTPUT[10], OUTPUT[11], OUTPUT[12], OUTPUT[13], OUTPUT[14], OUTPUT[15], OUTPUT[8]);
  Multiplexer #(.enable("false")) multiplexer_2 (.in0(nor_1_out), .in1(1'b1), .out(ZERO), .sel(jFunctoin));
endmodule

module ALU_Control (
  input  [7:0] IMM,
  input  [2:0] ALUOp,
  output [1:0] FUNCTION
);

  wire and_1_out, and_2_out, and_3_out, not_1_out, not_2_out;
  wire [1:0] multiplexer_1_out;

  Multiplexer #(.width(2), .enable("false")) multiplexer_1 (
    .in0(2'b00), .in1(IMM[1:0]), .out(multiplexer_1_out), .sel(ALUOp[2]));
  not not_1 (not_1_out, ALUOp[0]);
  not not_2 (not_2_out, ALUOp[1]);
  and and_1 (and_1_out, not_1_out, not_2_out);
  and and_2 (and_2_out, multiplexer_1_out[0], and_1_out, not_1_out);
  and and_3 (and_3_out, multiplexer_1_out[1], and_1_out, not_2_out);
  or or_1 (FUNCTION[0], ALUOp[0], and_2_out);
  or or_2 (FUNCTION[1], and_3_out, ALUOp[1]);
endmodule

module general_circuit (
  input  reset,
  output [1:0] out_2,
  output [15:0] out_3,
  output [15:0] out_4,
  output [1:0] out_5,
  output [1:0] out_6
);

  wire ALU_zero, and_1_out, and_2_out, Clock_out, Main_Control_alusrca, Main_Control_iord,
       Main_Control_irwrite, Main_Control_jfunction, Main_Control_memread, Main_Control_memtoreg,
       Main_Control_memwrite, Main_Control_pcwrite, Main_Control_pcwritecond, Main_Control_regdst,
       Main_Control_regwrite, not_1_out, not_2_out, not_3_out, not_4_out, or_1_out;
  wire [1:0] multiplexer_2_out;
  wire [2:0] Main_Control_aluop;
  wire [15:0] A_q, ALU_output, ALUOut_2_q, and_3_out, B_q, bit_extender_1_out, bit_extender_2_out, memory_dr,
       memory_ir, multiplexer_1_out, multiplexer_3_out, multiplexer_6_out, or_2_out, pc_1_out,
       registerSet_out1, registerSet_out2, registerSet_reg0, registerSet_reg1, registerSet_reg2,
       registerSet_reg3;

  Clock Clock (.out(Clock_out));
  and and_1 (and_1_out, or_1_out, not_1_out);
  not not_1 (not_1_out, Clock_out);
  PC pc_1 (.IN(multiplexer_6_out), .PCControl(and_1_out), .clock(Clock_out), .OUT(pc_1_out), .RESET(reset));
  not not_2 (not_2_out, Clock_out);
  or or_1 (or_1_out, and_2_out, Main_Control_pcwrite);
  Multiplexer #(.width(16), .enable("false")) multiplexer_1 (
    .in0(pc_1_out), .in1(ALUOut_2_q), .out(multiplexer_1_out), .sel(Main_Control_iord));
  Register #(.width(16), .trigger("high")) \u_下一个PC  (.D(pc_1_out), .en(1'b1), .clk(1'b1));  // open: Q, clr
  Register #(.width(16), .trigger("high")) \u_指令  (.D(memory_ir), .en(1'b1), .clk(1'b1));  // open: Q, clr
  and and_2 (and_2_out, ALU_zero, Main_Control_pcwritecond);
  memory memory (
    .AD_IN(multiplexer_1_out), .VALUE_IN(B_q), .IRWrite(Main_Control_irwrite),
    .MemWrite(Main_Control_memwrite), .clock(Clock_out), .MemRead(Main_Control_memread), .IR(memory_ir),
    .DR(memory_dr));
  Main_Control Main_Control (
    .clock(Clock_out), .OPCode(memory_ir[15:12]), .PCWriteCond(Main_Control_pcwritecond),
    .PCWrite(Main_Control_pcwrite), .PCSource(out_2), .IorD(Main_Control_iord),
    .MemWrite(Main_Control_memwrite), .MemRead(Main_Control_memread), .MemtoReg(Main_Control_memtoreg),
    .RegDst(Main_Control_regdst), .RegWrite(Main_Control_regwrite), .IRWrite(Main_Control_irwrite),
    .ALUSrcB(out_5), .ALUSrcA(Main_Control_alusrca), .ALUOp(Main_Control_aluop),
    .jFunction(Main_Control_jfunction));
  Register #(.width(16), .trigger("high")) \u_数据  (.D(memory_dr), .en(1'b1), .clk(1'b1));  // open: Q, clr
  assign bit_extender_1_out = {{4{1'b0}}, memory_ir[11:0]};  // Bit_Extender bit_extender_1
  Multiplexer #(.width(2), .enable("false")) multiplexer_2 (
    .in0(memory_ir[9:8]), .in1(memory_ir[7:6]), .out(multiplexer_2_out), .sel(Main_Control_regdst));
  Multiplexer #(.width(16), .enable("false")) multiplexer_3 (
    .in0(ALUOut_2_q), .in1(memory_dr), .out(multiplexer_3_out), .sel(Main_Control_memtoreg));
  Register #(.width(16), .trigger("high")) ALUOut (.D(ALUOut_2_q), .en(1'b1), .clk(1'b1));  // open: Q, clr
  registerSet registerSet (
    .link_WR(multiplexer_3_out), .selectR(multiplexer_2_out), .RegWrite(Main_Control_regwrite),
    .reg3(registerSet_reg3), .reg2(registerSet_reg2), .selectRA(memory_ir[11:10]), .selectRB(memory_ir[9:8]),
    .out1(registerSet_out1), .out2(registerSet_out2), .reg0(registerSet_reg0), .reg1(registerSet_reg1));
  Register #(.width(16), .trigger("high")) reg3 (.D(registerSet_reg3), .en(1'b1), .clk(1'b1));  // open: Q, clr
  Register #(.width(16)) A (.D(registerSet_out1), .en(not_2_out), .Q(A_q), .clk(not_2_out));  // open: clr
  Register #(.width(16)) B (.D(registerSet_out2), .en(not_2_out), .Q(B_q), .clk(not_2_out));  // open: clr
  assign bit_extender_2_out = {{8{1'b0}}, memory_ir[7:0]};  // Bit_Extender bit_extender_2
  Register #(.width(16), .trigger("high")) reg2 (.D(registerSet_reg2), .en(1'b1), .clk(1'b1));  // open: Q, clr
  Multiplexer #(.width(16), .enable("false")) multiplexer_4 (
    .in0(pc_1_out), .in1(A_q), .out(out_3), .sel(Main_Control_alusrca));
  Multiplexer #(.select(2), .width(16), .enable("false")) multiplexer_5 (
    .in0(B_q), .in1(16'h1), .in2(bit_extender_2_out), .in3(bit_extender_2_out), .out(out_4), .sel(out_5));
  ALU_Control ALU_Control (.IMM(memory_ir[7:0]), .ALUOp(Main_Control_aluop), .FUNCTION(out_6));
  Register #(.width(16), .trigger("high")) reg1 (.D(registerSet_reg1), .en(1'b1), .clk(1'b1));  // open: Q, clr
  ALU ALU (
    .IN1(out_3), .IN2(out_4), .jFunctoin(Main_Control_jfunction), .OUTPUT(ALU_output), .ZERO(ALU_zero),
    .FUNCTION(out_6));
  not not_3 (not_3_out, not_4_out);
  Register #(.width(16), .trigger("high")) reg0 (.D(registerSet_reg0), .en(1'b1), .clk(1'b1));  // open: Q, clr
  assign or_2_out = bit_extender_1_out | and_3_out;  // OR_Gate or_2, 16 bits wide
  assign and_3_out = pc_1_out & 16'hf000;  // AND_Gate and_3, 16 bits wide
  Register #(.width(16)) ALUOut_2 (.D(ALU_output), .en(not_3_out), .Q(ALUOut_2_q), .clk(not_4_out));  // open: clr
  not not_4 (not_4_out, not_2_out);
  Multiplexer #(.select(2), .width(16), .enable("false")) multiplexer_6 (
    .in0(ALU_output), .in1(ALUOut_2_q), .in2(or_2_out), .out(multiplexer_6_out), .sel(out_2));  // open: in3

  // Notes on the sheet:
  //   总时钟
  //   LorD
  //   MenWrite
  //   MenRead
  //   主控制器
  //   IRWrite
  //   RegWrite
  //   MemtoReg
  //   RegDst
  //   jFunction
  //   ALUSrcA
  //   ALUSrcB
  //   ALUOp
  //   PCSource
endmodule

module PC (
  input  [15:0] IN,
  input  PCControl,
  input  clock,
  input  RESET,
  output [15:0] OUT
);

  Register #(.width(16)) register_1 (.D(IN), .en(PCControl), .Q(OUT), .clk(clock), .clr(RESET));
endmodule

module Main_Control (
  input  clock,
  input  [3:0] OPCode,
  output PCWriteCond,
  output PCWrite,
  output [1:0] PCSource,
  output IorD,
  output MemWrite,
  output MemRead,
  output MemtoReg,
  output RegDst,
  output RegWrite,
  output IRWrite,
  output [1:0] ALUSrcB,
  output ALUSrcA,
  output [2:0] ALUOp,
  output jFunction
);

  wire [1:0] rom_1_data;
  wire [7:0] adder_1_out, multiplexer_1_out, register_1_q, rom_2_data, rom_3_data;

  Register register_1 (.D(multiplexer_1_out), .en(clock), .Q(register_1_q), .clk(clock));  // open: clr
  Multiplexer #(.select(2), .width(8), .enable("false")) multiplexer_1 (
    .in0({8{1'b0}}), .in1(rom_2_data), .in2(rom_3_data), .in3(adder_1_out), .out(multiplexer_1_out),
    .sel(rom_1_data));
  ROM #(.dataWidth(20)) rom_1 (
    .addr(register_1_q),
    .data({jFunction, ALUOp, ALUSrcA, ALUSrcB, IRWrite, RegWrite, RegDst, MemtoReg, MemRead, MemWrite, IorD, PCSource, PCWrite, PCWriteCond, rom_1_data}));  // open: sel
  ROM #(.addrWidth(4)) rom_2 (.addr(OPCode), .data(rom_2_data));  // open: sel
  Adder adder_1 (.a(register_1_q), .b(8'h1), .out(adder_1_out));  // open: cin, cout
  ROM #(.addrWidth(4)) rom_3 (.addr(OPCode), .data(rom_3_data));  // open: sel

  // Notes on the sheet:
  //   Sequncing
  //   contents of rom_1 (hex, n*v repeats v):
  //   3 310b 6001 c002 343 a00 c0 48403 c00 18014 28 3c033 c00 c033 c00 2c033 c00 98014
  //   contents of rom_2 (hex, n*v repeats v):
  //   7 0 0 b d f 3 3 a 9 11
  //   Dispatch ROM 1
  //   contents of rom_3 (hex, n*v repeats v):
  //   6*0 4 6
  //   Dispatch ROM  2
endmodule

module extend (
  input  [15:0] in_1,
  output [7:0] out_2,
  output [7:0] out_3,
  output [7:0] out_4,
  output [7:0] out_5
);

  assign out_2 = {{4{1'b0}}, in_1[15:12]};  // Bit_Extender bit_extender_1
  assign out_5 = {{4{1'b0}}, in_1[11:8]};  // Bit_Extender bit_extender_2
  assign out_3 = {{4{1'b0}}, in_1[7:4]};  // Bit_Extender bit_extender_3
  assign out_4 = {{4{1'b0}}, in_1[3:0]};  // Bit_Extender bit_extender_4
endmodule
