// Logisim project CS1503_U201514559_周铭昊_CPU.circ as structural Verilog: 7 circuits, main circuit cpu
module cpu (
);

  wire alu_1_p4, ALUsrc, and_2_out, and_3_out, and_4_out, and_5_out, and_6_out, and_7_out, and_8_out,
       and_9_out, beq, blez, bne, CLK, comparator_1_eq, comparator_2_eq, comparator_3_gt, comparator_4_eq,
       correct_b, halt, IR1, IR2, IR3, j, jal, jr, MemToReg, Memwrite, not_1_out, not_2_out, not_3_out,
       not_4_out, not_5_out, not_6_out, not_7_out, not_8_out, or_2_out, or_3_out, or_4_out, RegDst,
       register_2_q, RegWrite, RST, sh, Syscall, W1, W2, W3;
  wire [1:0] EXTOP;
  wire [3:0] ALUOP;
  wire [4:0] decoder_1__10_6, decoder_1__15_11, decoder_1__20_16, decoder_1__25_21, multiplexer_1_out,
       multiplexer_2_out, multiplexer_3_out, multiplexer_4_out, multiplexer_5_out;
  wire [5:0] decoder_1_func_5_0, decoder_1_op_31_26;
  wire [15:0] decoder_1__15_0, \load_use次数 , \总周期数 , \插入气泡数 , \无条件分支指令数 , \有条件分支成功跳转 , \有条件分支指令数 ;
  wire [31:0] adder_1_out, adder_2_out, adder_3_out, alu_1_p2, alu_1_p5, extender_1_out_4, index,
       multiplexer_7_out, multiplexer_9_out, multiplexer_10_out, multiplexer_11_out, multiplexer_12_out,
       multiplexer_13_out, multiplexer_14_out, PC_q, ram_1_data, register_1_q, registerfile_1_p1, RF_A, RF_B,
       rom_1_data, SyscallOut, undriven, undriven_2;

  Button \u_总复位  (.out(RST));
  Clock clock_1 (.out(CLK));
  Button _1 (.out(IR1));
  Button _2 (.out(IR2));
  Button _3 (.out(IR3));
  LED led_1 (.in(W1));
  LED led_2 (.in(W2));
  LED led_3 (.in(W3));
  Hex_Digit_Display hex_digit_display_1 (.value(SyscallOut[31:28]));  // open: dp
  not not_1 (not_1_out, halt);
  Hex_Digit_Display hex_digit_display_2 (.value(SyscallOut[23:20]));  // open: dp
  Hex_Digit_Display hex_digit_display_3 (.value(SyscallOut[27:24]));  // open: dp
  Register #(.width(32)) PC (.D(multiplexer_9_out), .en(not_1_out), .Q(PC_q), .clk(CLK), .clr(RST));
  Hex_Digit_Display hex_digit_display_4 (.value(SyscallOut[15:12]));  // open: dp
  Hex_Digit_Display hex_digit_display_5 (.value(SyscallOut[19:16]));  // open: dp
  Hex_Digit_Display hex_digit_display_6 (.value(SyscallOut[7:4]));  // open: dp
  Hex_Digit_Display hex_digit_display_7 (.value(SyscallOut[11:8]));  // open: dp
  ROM #(.addrWidth(10), .dataWidth(32)) rom_1 (.addr(PC_q[9:0]), .data(rom_1_data));  // open: sel
  Hex_Digit_Display hex_digit_display_8 (.value(SyscallOut[3:0]));  // open: dp
  Adder #(.width(32)) adder_1 (.a(32'h1), .b(PC_q), .out(adder_1_out));  // open: cin, cout
  decoder decoder_1 (
    .index(index), .in_1(rom_1_data), .op_31_26(decoder_1_op_31_26), ._25_21(decoder_1__25_21),
    ._20_16(decoder_1__20_16), .func_5_0(decoder_1_func_5_0), ._10_6(decoder_1__10_6),
    ._15_11(decoder_1__15_11), ._15_0(decoder_1__15_0));
  controller controller_1 (
    .func(decoder_1_func_5_0), .op(decoder_1_op_31_26), .RegDst(RegDst), .ALUsrc(ALUsrc), .blez(blez),
    .MemWrite(Memwrite), .RegWrite(RegWrite), .ALUOP(ALUOP), .MemToReg(MemToReg), .EXTOP(EXTOP), .beq(beq),
    .bne(bne), .j(j), .jal(jal), .jr(jr), .Syscall(Syscall), .sh(sh));
  // Probe on \总周期数 
  // Probe on \无条件分支指令数 
  // Probe on \有条件分支指令数 
  // Probe on \有条件分支成功跳转 
  // Probe on \load_use次数 
  // Probe on \插入气泡数 
  Comparator #(.width(2), .mode("unsigned")) comparator_1 (.a(EXTOP), .b(2'b10), .eq(comparator_1_eq));  // open: gt, lt
  extender extender_1 (.in_1(decoder_1__15_0), .in_3(decoder_1__10_6), .out_4(extender_1_out_4), .in_2(EXTOP));
  Multiplexer #(.width(5), .enable("false")) multiplexer_1 (
    .in0(decoder_1__25_21), .in1(decoder_1__20_16), .out(multiplexer_1_out), .sel(comparator_1_eq));
  Multiplexer #(.width(5), .enable("false")) multiplexer_2 (
    .in0(multiplexer_1_out), .in1(5'b00010), .out(multiplexer_2_out), .sel(Syscall));
  Multiplexer #(.width(5), .enable("false")) multiplexer_3 (
    .in0(decoder_1__20_16), .in1(decoder_1__15_11), .out(multiplexer_3_out), .sel(RegDst));
  Multiplexer #(.width(5), .enable("false")) multiplexer_4 (
    .in0(decoder_1__20_16), .in1(5'b00100), .out(multiplexer_4_out), .sel(Syscall));
  Multiplexer #(.width(5), .enable("false")) multiplexer_5 (
    .in0(multiplexer_3_out), .in1({5{1'b1}}), .out(multiplexer_5_out), .sel(jal));
  // RegisterFile registerfile_1: pin names not known; wires that end beside it: registerfile_1_p1, CLK, RegWrite, multiplexer_5_out, multiplexer_2_out, multiplexer_4_out, RF_A, RF_B
  Comparator #(.width(32)) comparator_2 (.a(RF_A), .b(32'ha), .eq(comparator_2_eq));  // open: gt, lt
  and and_1 (halt, comparator_2_eq, Syscall);
  // ALU alu_1: pin names not known; wires that end beside it: RF_A, alu_1_p2, ALUOP, alu_1_p4, alu_1_p5
  Multiplexer #(.width(32), .enable("false")) multiplexer_6 (
    .in0(RF_B), .in1(extender_1_out_4), .out(alu_1_p2), .sel(ALUsrc));
  or or_1 (correct_b, and_2_out, and_3_out, and_4_out);
  Multiplexer #(.width(32), .enable("false")) multiplexer_7 (
    .in0(adder_1_out), .in1(adder_2_out), .out(multiplexer_7_out), .sel(correct_b));
  Adder #(.width(32)) adder_2 (.a(adder_1_out), .b(extender_1_out_4), .out(adder_2_out));  // open: cin, cout
  and and_2 (and_2_out, alu_1_p4, beq);
  and and_3 (and_3_out, not_2_out, bne);
  and and_4 (and_4_out, not_3_out, blez);
  not not_2 (not_2_out, alu_1_p4);
  not not_3 (not_3_out, comparator_3_gt);
  Comparator #(.width(32), .mode("unsigned")) comparator_3 (
    .a(RF_A), .b({32{1'b0}}), .gt(comparator_3_gt));  // open: eq, lt
  Counter #(.width(16), .max('hffff)) counter_1 (
    .D(16'h1), .Q(\无条件分支指令数 ), .clk(and_5_out), .clr(RST));  // open: load, count, carry
  and and_5 (and_5_out, or_2_out, not_4_out);
  or or_2 (or_2_out, j, jal, jr);
  Multiplexer #(.width(32), .enable("false")) multiplexer_8 (
    .in0(multiplexer_10_out), .in1(adder_1_out), .out(registerfile_1_p1), .sel(jal));
  not not_4 (not_4_out, CLK);
  Multiplexer #(.width(32), .enable("false")) multiplexer_9 (
    .in0(multiplexer_12_out), .in1(RF_A), .out(multiplexer_9_out), .sel(jr));
  Multiplexer #(.width(32), .enable("false")) multiplexer_10 (
    .in0(alu_1_p5), .in1(ram_1_data), .out(multiplexer_10_out), .sel(MemToReg));
  Multiplexer #(.width(32), .enable("false")) multiplexer_11 (
    .in0(RF_B), .in1({{16{1'b0}}, RF_B[15:0]}), .out(multiplexer_11_out), .sel(sh));
  and and_6 (and_6_out, or_3_out, not_5_out);
  or or_3 (or_3_out, blez, beq, bne);
  or or_4 (or_4_out, j, jal);
  Multiplexer #(.width(32), .enable("false")) multiplexer_12 (
    .in0(multiplexer_13_out), .in1(index), .out(multiplexer_12_out), .sel(or_4_out));
  Adder #(.width(32)) adder_3 (.a(undriven), .b(undriven_2), .out(adder_3_out));  // open: cin, cout
  Counter #(.width(16), .max('hffff)) counter_2 (
    .D(16'h1), .Q(\有条件分支指令数 ), .clk(and_6_out), .clr(RST));  // open: load, count, carry
  not not_5 (not_5_out, CLK);
  Multiplexer #(.width(32), .enable("false")) multiplexer_13 (
    .in0(undriven), .in1(adder_3_out), .out(multiplexer_13_out));  // open: sel
  RAM #(.addrWidth(16), .dataWidth(32), .bus("separate")) ram_1 (
    .addr(alu_1_p5[15:0]), .din(multiplexer_11_out), .data(ram_1_data), .str(Memwrite), .clk(CLK),
    .ld(MemToReg), .clr(RST));  // open: sel
  not not_6 (not_6_out, comparator_4_eq);
  Comparator #(.width(32), .mode("unsigned")) comparator_4 (.a(RF_A), .b(32'ha), .eq(comparator_4_eq));  // open: gt, lt
  and and_7 (and_7_out, not_6_out, Syscall);
  Counter #(.width(16), .max('hffff)) counter_3 (
    .D(16'h1), .Q(\有条件分支成功跳转 ), .clk(and_8_out), .clr(RST));  // open: load, count, carry
  and and_8 (and_8_out, correct_b, not_7_out);
  Multiplexer #(.width(32), .enable("false")) multiplexer_14 (
    .in0(register_1_q), .in1(RF_B), .out(multiplexer_14_out), .sel(and_7_out));
  not not_7 (not_7_out, CLK);
  Register #(.width(32)) register_1 (.D(multiplexer_14_out), .en(1'b1), .Q(register_1_q), .clk(CLK), .clr(RST));
  Multiplexer #(.width(32), .enable("false")) multiplexer_15 (
    .in0(register_1_q), .in1(multiplexer_14_out), .out(SyscallOut), .sel(and_7_out));
  Register #(.width(1)) register_2 (.D(not_8_out), .Q(register_2_q), .clk(CLK), .clr(RST));  // open: en
  not not_8 (not_8_out, halt);
  Counter #(.width(16), .max('hffff)) counter_4 (
    .D(16'h1), .Q(\总周期数 ), .clk(and_9_out), .clr(RST));  // open: load, count, carry
  and and_9 (and_9_out, register_2_q, CLK);

  // Notes on the sheet:
  //   指令存储器
  //   contents of rom_1 (hex, n*v repeats v):
  //   20110001 8000c05 20110001 20120002 20130003 8000c09 20110001 20120002 20130003 8000c0d 20110001
  //   20120002 20130003 8000c11 20110001 20120002 20130003 c000cb8 20100001 20110001 118fc0 112020
  //   20020022 c 118882 12200001 8000c15 112020 20020022 c 20110001 118880 112020 20020022 c 12200001
  //   8000c1f 20110001 118fc0 112020 20020022 c 1188c3 112020 20020022 c 118903 112020 20020022 c 118903
  //   112020 20020022 c 118903 112020 20020022 c 118903 112020 20020022 c 118903 112020 20020022 c 118903
  //   112020 20020022 c 118903 112020 20020022 c 20100001 109fc0 139fc3 8021 2012000c 24160003 26100001
  //   3210000f 20080008 20090001 139900 2709825 132020 20020022 c 1094022 1500fff9 22100001 2018000f
  //   2188024 108700 20080008 20090001 139902 2709825 132021 20020022 c 1094022 1500fff9 108702 2c9b022
  //   12c00001 8000c50 4020 1084027 84400 3508ffff 82021 20020022 c 2010ffff 20110000 ae300000 22100001
  //   22310004 ae300000 22100001 22310004 ae300000 22100001 22310004 ae300000 22100001 22310004 ae300000
  //   22100001 22310004 ae300000 22100001 22310004 ae300000 22100001 22310004 ae300000 22100001 22310004
  //   ae300000 22100001 22310004 ae300000 22100001 22310004 ae300000 22100001 22310004 ae300000 22100001
  //   22310004 ae300000 22100001 22310004 ae300000 22100001 22310004 ae300000 22100001 22310004 ae300000
  //   22100001 22310004 22100001 8020 2011003c 8e130000 8e340000 274402a 11000002 ae330000 ae140000
  //   2231fffc 1611fff8 102020 20020022 c 22100004 2011003c 1611fff2 2002000a c 20100000 22100001 102020
  //   20020022 c 22100002 102020 20020022 c 22100003 102020 20020022 c 22100004 102020 20020022 c 22100005
  //   102020 20020022 c 22100006 102020 20020022 c 22100007 102020 20020022 c 22100008 102020 20020022
  //   20020022 c 3e00008
  //   数码管输出
  //   译码器
  //   控制器
  //   [25:21]
  //   [20:16]
  //   15:11
  //   位扩展
  //   寄存器文件
  //   数据存储器
endmodule

module controller (
  input  [5:0] func,
  input  [5:0] op,
  output RegDst,
  output ALUsrc,
  output RegWrite,
  output MemToReg,
  output MemWrite,
  output [1:0] EXTOP,
  output blez,
  output beq,
  output bne,
  output j,
  output jal,
  output jr,
  output Syscall,
  output [3:0] ALUOP,
  output sh
);

  wire add, add_out, addi_out, addiu_out, addu_out, \and , and_out, andi_out, \nor , not_1_out, not_2_out,
       not_3_out, not_4_out, not_5_out, not_6_out, not_7_out, not_8_out, not_9_out, not_10_out, not_11_out,
       not_12_out, not_13_out, not_14_out, not_15_out, not_16_out, not_17_out, not_18_out, not_19_out,
       not_20_out, not_21_out, not_22_out, not_23_out, \or , or_out, sll, slt, slt_out, slti_out, sltiu_out,
       sltu, sltu_out, sra, srl, sub, sw_out, \xor ;

  not not_1 (not_1_out, func[5]);
  not not_2 (not_2_out, func[3]);
  not not_3 (not_3_out, func[4]);
  not not_4 (not_4_out, func[2]);
  not not_5 (not_5_out, func[1]);
  not not_6 (not_6_out, func[0]);
  not not_7 (not_7_out, op[4]);
  not not_8 (not_8_out, op[5]);
  not not_9 (not_9_out, op[2]);
  not not_10 (not_10_out, op[3]);
  not not_11 (not_11_out, op[0]);
  not not_12 (not_12_out, op[1]);
  and u_add (add_out, not_8_out, not_7_out, not_10_out, not_9_out, not_12_out, not_11_out, func[5], not_3_out, not_2_out, not_4_out, not_5_out, not_6_out);
  and addi (addi_out, not_8_out, not_7_out, op[3], not_9_out, not_12_out, not_11_out);
  and addiu (addiu_out, not_8_out, not_7_out, op[3], not_9_out, not_12_out, op[0]);
  and addu (addu_out, not_8_out, not_7_out, not_10_out, not_9_out, not_12_out, not_11_out, func[5], not_3_out, not_2_out, not_4_out, not_5_out, func[0]);
  and u_and (and_out, not_8_out, not_7_out, not_10_out, not_9_out, not_12_out, not_11_out, func[5], not_3_out, not_2_out, func[2], not_5_out, not_6_out);
  and andi (andi_out, not_8_out, not_7_out, op[3], op[2], not_12_out, not_11_out);
  and u_sll (sll, not_8_out, not_7_out, not_10_out, not_9_out, not_12_out, not_11_out, not_1_out, not_3_out, not_2_out, not_4_out, not_5_out, not_6_out);
  and u_sra (sra, not_8_out, not_7_out, not_10_out, not_9_out, not_12_out, not_11_out, not_1_out, not_3_out, not_2_out, not_4_out, func[1], func[0]);
  and u_srl (srl, not_8_out, not_7_out, not_10_out, not_9_out, not_12_out, not_11_out, not_1_out, not_3_out, not_2_out, not_4_out, func[1], not_6_out);
  and u_sub (sub, not_8_out, not_7_out, not_10_out, not_9_out, not_12_out, not_11_out, func[5], not_3_out, not_2_out, not_4_out, func[1], not_6_out);
  and u_or (or_out, not_8_out, not_7_out, not_10_out, not_9_out, not_12_out, not_11_out, func[5], not_3_out, not_2_out, func[2], not_5_out, func[0]);
  and ori (EXTOP[0], not_8_out, not_7_out, op[3], op[2], not_12_out, op[0]);
  and u_nor (\nor , not_8_out, not_7_out, not_10_out, not_9_out, not_12_out, not_11_out, func[5], not_3_out, not_2_out, func[2], func[1], func[0]);
  and lw (MemToReg, op[5], not_7_out, not_10_out, not_9_out, op[1], op[0]);
  and sw (sw_out, op[5], not_7_out, op[3], not_9_out, op[1], op[0]);
  and u_beq (beq, not_8_out, not_7_out, not_10_out, op[2], not_12_out, not_11_out);
  and u_bne (bne, not_8_out, not_7_out, not_10_out, op[2], not_12_out, op[0]);
  and u_slt (slt_out, not_8_out, not_7_out, not_10_out, not_9_out, not_12_out, not_11_out, func[5], not_3_out, func[3], not_4_out, func[1], not_6_out);
  and slti (slti_out, not_8_out, not_7_out, op[3], not_9_out, op[1], not_11_out);
  and u_sltu (sltu_out, not_8_out, not_7_out, not_10_out, not_9_out, not_12_out, not_11_out, func[5], not_3_out, func[3], not_4_out, func[1], func[0]);
  and u_j (j, not_8_out, not_7_out, not_10_out, not_9_out, op[1], not_11_out);
  and u_jal (jal, not_8_out, not_7_out, not_10_out, not_9_out, op[1], op[0]);
  and u_jr (jr, not_8_out, not_7_out, not_10_out, not_9_out, not_12_out, not_11_out, not_1_out, not_3_out, func[3], not_4_out, not_5_out, not_6_out);
  and u_syscall (Syscall, not_8_out, not_7_out, not_10_out, not_9_out, not_12_out, not_11_out, not_1_out, not_3_out, func[3], func[2], not_5_out, not_6_out);
  and u_xor (\xor , not_8_out, not_7_out, not_10_out, not_9_out, not_12_out, not_11_out, func[5], not_3_out, not_2_out, func[2], func[1], not_6_out);
  and sltiu (sltiu_out, not_8_out, not_7_out, op[3], not_9_out, op[1], op[0]);
  and u_sh (sh, op[5], not_7_out, op[3], not_9_out, not_12_out, op[0]);
  and u_blez (blez, not_8_out, not_7_out, not_10_out, op[2], op[1], not_11_out);
  or or_2 (RegDst, add_out, addu_out, and_out, sll, sra, srl, sub, or_out, \nor , slt_out, sltu_out, \xor );
  or or_3 (ALUsrc, addi_out, addiu_out, andi_out, sll, sra, srl, EXTOP[0], MemToReg, sw_out, slti_out, sltiu_out, sh);
  or or_4 (RegWrite, add_out, addi_out, addiu_out, addu_out, and_out, andi_out, sll, sra, srl, sub, or_out, EXTOP[0], \nor , MemToReg, slt_out, slti_out, sltu_out, jal, \xor , sltiu_out);
  or or_5 (MemWrite, sw_out, sh);
  or or_6 (EXTOP[1], sll, sra, srl);
  or and_2 (\and , and_out, andi_out);
  or or_7 (\or , or_out, EXTOP[0]);
  or slt_2 (slt, slt_out, slti_out);
  or ALUOP3 (ALUOP[3], \or , \xor , \nor , slt, sltu);
  or ALUOP2 (ALUOP[2], add, sub, \and , sltu);
  or ALUOP1 (ALUOP[1], srl, sub, \and , \nor , slt);
  or ALUOP0 (ALUOP[0], sra, add, \and , \xor , slt);
  or sltu_2 (sltu, sltu_out, sltiu_out);
  not not_13 (not_13_out, sra);
  not not_14 (not_14_out, sll);
  or add_2 (add, add_out, addi_out, addiu_out, addu_out, MemToReg, sw_out, sh);
  not not_15 (not_15_out, add);
  not not_16 (not_16_out, srl);
  not not_17 (not_17_out, \and );
  not not_18 (not_18_out, sub);
  not not_19 (not_19_out, \or );
  not not_20 (not_20_out, \xor );
  not not_21 (not_21_out, slt);
  not not_22 (not_22_out, \nor );
  not not_23 (not_23_out, sltu);
endmodule

module decoder (
  input  [31:0] in_1,
  output [31:0] index,
  output [5:0] op_31_26,
  output [4:0] _25_21,
  output [4:0] _20_16,
  output [15:0] _15_0,
  output [5:0] func_5_0,
  output [4:0] _10_6,
  output [4:0] _15_11
);


  assign _10_6 = in_1[10:6];
  assign _15_0 = in_1[15:0];
  assign _15_11 = in_1[15:11];
  assign _20_16 = in_1[20:16];
  assign _25_21 = in_1[25:21];
  assign func_5_0 = in_1[5:0];
  assign index = {{6{1'b0}}, in_1[25:0]};
  assign op_31_26 = in_1[31:26];

  // Notes on the sheet:
  //   指令
endmodule

module extender (
  input  [15:0] in_1,
  input  [1:0] in_2,
  input  [4:0] in_3,
  output [31:0] out_4
);

  wire [31:0] bit_extender_1_out, bit_extender_2_out, bit_extender_3_out;

  assign bit_extender_1_out = {{16{in_1[15]}}, in_1};  // Bit_Extender bit_extender_1
  assign bit_extender_2_out = {{16{1'b0}}, in_1};  // Bit_Extender bit_extender_2
  assign bit_extender_3_out = {{27{1'b0}}, in_3};  // Bit_Extender bit_extender_3
  Multiplexer #(.select(2), .width(32), .enable("false")) multiplexer_1 (
    .in0(bit_extender_1_out), .in1(bit_extender_2_out), .in2(bit_extender_3_out), .in3({32{1'b0}}),
    .out(out_4), .sel(in_2));

  // Notes on the sheet:
  //   [15:0]
  //   [10:6]
endmodule

module npc (
  input  \是否相等 ,
  input  [31:0] RF_A,
  input  beq,
  input  bne,
  input  [31:0] PC_1,
  input  blez,
  input  [31:0] ext,
  input  j,
  input  jal,
  input  [31:0] index,
  input  jr,
  output correct_b,
  output [31:0] out_13
);

  wire and_1_out, and_2_out, and_3_out, comparator_1_gt, not_1_out, not_2_out, or_2_out;
  wire [31:0] adder_1_out, multiplexer_2_out, multiplexer_3_out;

  Multiplexer #(.width(32), .enable("false")) multiplexer_1 (
    .in0(multiplexer_2_out), .in1(RF_A), .out(out_13), .sel(jr));
  Adder #(.width(32)) adder_1 (.a(PC_1), .b(ext), .out(adder_1_out));  // open: cin, cout
  Multiplexer #(.width(32), .enable("false")) multiplexer_2 (
    .in0(multiplexer_3_out), .in1(index), .out(multiplexer_2_out), .sel(or_2_out));
  or or_1 (correct_b, and_1_out, and_2_out, and_3_out);
  Multiplexer #(.width(32), .enable("false")) multiplexer_3 (
    .in0(PC_1), .in1(adder_1_out), .out(multiplexer_3_out), .sel(correct_b));
  or or_2 (or_2_out, j, jal);
  and and_1 (and_1_out, \是否相等 , beq);
  and and_2 (and_2_out, not_1_out, bne);
  not not_1 (not_1_out, \是否相等 );
  and and_3 (and_3_out, not_2_out, blez);
  not not_2 (not_2_out, comparator_1_gt);
  Comparator #(.width(32), .mode("unsigned")) comparator_1 (
    .a(RF_A), .b({32{1'b0}}), .gt(comparator_1_gt));  // open: eq, lt
endmodule

module IF_ID (
  input  [31:0] PC_4,
  input  [31:0] \指令 ,
  input  in_3,
  input  in_4,
  output [31:0] PC_4_2,
  output [31:0] \指令_2 
);

  wire [31:0] multiplexer_1_out, multiplexer_2_out;

  Multiplexer #(.width(32), .enable("false")) multiplexer_1 (
    .in0(PC_4), .in1({32{1'b0}}), .out(multiplexer_1_out), .sel(in_3));
  Multiplexer #(.width(32), .enable("false")) multiplexer_2 (
    .in0(\指令 ), .in1({32{1'b0}}), .out(multiplexer_2_out), .sel(in_3));
  Register #(.width(32)) register_1 (.D(multiplexer_1_out), .Q(PC_4_2), .clk(in_4));  // open: en, clr
  Register #(.width(32)) register_2 (.D(multiplexer_2_out), .Q(\指令_2 ), .clk(in_4));  // open: en, clr

  // Other names for the same wires on the sheet: CLK = in_4; RST = in_3
endmodule

module ID_EX (
  input  in_1,
  input  in_2,
  input  [31:0] PC_4,
  input  [31:0] \指令 ,
  input  RegDst,
  input  ALUsrc,
  input  RegWrite,
  input  MemToReg,
  input  MemWrite,
  input  [1:0] EXTOP,
  input  blez,
  input  beq,
  input  bne,
  input  j,
  input  jal,
  input  jr,
  input  Syscall,
  input  [3:0] ALUOP,
  output [31:0] PC_4_2,
  output [31:0] \指令_2 ,
  output RegDst_2,
  output ALUsrc_2,
  output RegWrite_2,
  output MemToReg_2,
  output MemWrite_2,
  output [1:0] EXTOP_2,
  output blez_2,
  output beq_2,
  output bne_2,
  output j_2,
  output jal_2,
  output jr_2,
  output Syscall_2,
  output [3:0] ALUOP_2
);

  wire multiplexer_3_out, multiplexer_4_out, multiplexer_5_out, multiplexer_6_out, multiplexer_7_out,
       multiplexer_9_out, multiplexer_10_out, multiplexer_11_out, multiplexer_12_out, multiplexer_13_out,
       multiplexer_14_out, multiplexer_15_out;
  wire [1:0] multiplexer_8_out;
  wire [3:0] multiplexer_16_out;
  wire [31:0] multiplexer_1_out, multiplexer_2_out;

  Multiplexer #(.width(32), .enable("false")) multiplexer_1 (
    .in0(PC_4), .in1({32{1'b0}}), .out(multiplexer_1_out), .sel(in_1));
  Multiplexer #(.width(32), .enable("false")) multiplexer_2 (
    .in0(\指令 ), .in1({32{1'b0}}), .out(multiplexer_2_out), .sel(in_1));
  Multiplexer #(.enable("false")) multiplexer_3 (.in0(RegDst), .in1(1'b0), .out(multiplexer_3_out), .sel(in_1));
  Multiplexer #(.enable("false")) multiplexer_4 (.in0(ALUsrc), .in1(1'b0), .out(multiplexer_4_out), .sel(in_1));
  Multiplexer #(.enable("false")) multiplexer_5 (.in0(RegWrite), .in1(1'b0), .out(multiplexer_5_out), .sel(in_1));
  Multiplexer #(.enable("false")) multiplexer_6 (.in0(MemToReg), .in1(1'b0), .out(multiplexer_6_out), .sel(in_1));
  Multiplexer #(.enable("false")) multiplexer_7 (.in0(MemWrite), .in1(1'b0), .out(multiplexer_7_out), .sel(in_1));
  Multiplexer #(.width(2), .enable("false")) multiplexer_8 (
    .in0(EXTOP), .in1(2'b00), .out(multiplexer_8_out), .sel(in_1));
  Multiplexer #(.enable("false")) multiplexer_9 (.in0(blez), .in1(1'b0), .out(multiplexer_9_out), .sel(in_1));
  Multiplexer #(.enable("false")) multiplexer_10 (.in0(beq), .in1(1'b0), .out(multiplexer_10_out), .sel(in_1));
  Multiplexer #(.enable("false")) multiplexer_11 (.in0(bne), .in1(1'b0), .out(multiplexer_11_out), .sel(in_1));
  Multiplexer #(.enable("false")) multiplexer_12 (.in0(j), .in1(1'b0), .out(multiplexer_12_out), .sel(in_1));
  Multiplexer #(.enable("false")) multiplexer_13 (.in0(jal), .in1(1'b0), .out(multiplexer_13_out), .sel(in_1));
  Multiplexer #(.enable("false")) multiplexer_14 (.in0(jr), .in1(1'b0), .out(multiplexer_14_out), .sel(in_1));
  Multiplexer #(.enable("false")) multiplexer_15 (.in0(Syscall), .in1(1'b0), .out(multiplexer_15_out), .sel(in_1));
  Multiplexer #(.width(4), .enable("false")) multiplexer_16 (
    .in0(ALUOP), .in1(4'b0000), .out(multiplexer_16_out), .sel(in_1));
  Register #(.width(32)) register_1 (.D(multiplexer_1_out), .Q(PC_4_2), .clk(in_2));  // open: en, clr
  Register #(.width(32)) register_2 (.D(multiplexer_2_out), .Q(\指令_2 ), .clk(in_2));  // open: en, clr
  Register #(.width(1)) register_3 (.D(multiplexer_3_out), .Q(RegDst_2), .clk(in_2));  // open: en, clr
  Register #(.width(1)) register_4 (.D(multiplexer_4_out), .Q(ALUsrc_2), .clk(in_2));  // open: en, clr
  Register #(.width(1)) register_5 (.D(multiplexer_5_out), .Q(RegWrite_2), .clk(in_2));  // open: en, clr
  Register #(.width(1)) register_6 (.D(multiplexer_6_out), .Q(MemToReg_2), .clk(in_2));  // open: en, clr
  Register #(.width(1)) register_7 (.D(multiplexer_7_out), .Q(MemWrite_2), .clk(in_2));  // open: en, clr
  Register #(.width(2)) register_8 (.D(multiplexer_8_out), .Q(EXTOP_2), .clk(in_2));  // open: en, clr
  Register #(.width(1)) register_9 (.D(multiplexer_9_out), .Q(blez_2), .clk(in_2));  // open: en, clr
  Register #(.width(1)) register_10 (.D(multiplexer_10_out), .Q(beq_2), .clk(in_2));  // open: en, clr
  Register #(.width(1)) register_11 (.D(multiplexer_11_out), .Q(bne_2), .clk(in_2));  // open: en, clr
  Register #(.width(1)) register_12 (.D(multiplexer_12_out), .Q(j_2), .clk(in_2));  // open: en, clr
  Register #(.width(1)) register_13 (.D(multiplexer_13_out), .Q(jal_2), .clk(in_2));  // open: en, clr
  Register #(.width(1)) register_14 (.D(multiplexer_14_out), .Q(jr_2), .clk(in_2));  // open: en, clr
  Register #(.width(1)) register_15 (.D(multiplexer_15_out), .Q(Syscall_2), .clk(in_2));  // open: en, clr
  Register #(.width(4)) register_16 (.D(multiplexer_16_out), .Q(ALUOP_2), .clk(in_2));  // open: en, clr

  // Other names for the same wires on the sheet: CLK = in_2; RST = in_1
endmodule
