// Logisim project CS1503_U201514559_周铭昊_CPU.circ as structural Verilog
module cpu (
);

  wire A_MEM, A_WB, add_2_out, add_out, addu_2_out, addu_out, alu_1_p4, ALUSrc, alusrc1, and_1_out,
       and_2_out, and_3_out, and_8_out, and_9_out, and_10_out, and_11_out, and_12_out, and_13_out,
       and_14_out, and_15_out, and_16_out, and_17_out, and_18_out, and_19_out, and_20_out, and_21_out,
       and_22_out, B_MEM, B_WB, beq, beq_2_out, beq_out, blez, bne, bne_2_out, bne_out, bub1, bub2, CLK,
       comparator_1_eq, comparator_2_eq, comparator_3_eq, comparator_4_eq, comparator_5_eq, comparator_6_eq,
       comparator_7_eq, comparator_8_eq, comparator_9_eq, comparator_10_eq, comparator_11_eq,
       comparator_12_eq, comparator_13_eq, comparator_14_eq, comparator_15_eq, comparator_16_eq,
       comparator_17_eq, comparator_18_eq, comparator_19_eq, comparator_20_eq, comparator_21_eq,
       comparator_22_eq, comparator_23_eq, comparator_24_eq, comparator_25_eq, comparator_26_eq,
       comparator_27_eq, comparator_28_eq, comparator_29_eq, comparator_30_eq, comparator_31_eq,
       comparator_32_eq, comparator_33_eq, comparator_34_eq, comparator_35_eq, comparator_36_eq,
       comparator_37_eq, comparator_38_eq, comparator_39_eq, comparator_40_eq, comparator_41_eq,
       comparator_42_eq, comparator_43_eq, comparator_44_eq, comparator_45_eq, comparator_46_eq,
       comparator_47_eq, comparator_48_eq, comparator_49_eq, comparator_50_eq, comparator_51_eq,
       comparator_52_eq, comparator_53_eq, comparator_54_eq, comparator_55_eq, comparator_56_eq,
       comparator_57_eq, comparator_58_eq, comparator_59_eq, comparator_60_eq, comparator_61_eq,
       comparator_62_eq, comparator_63_eq, comparator_64_eq, comparator_65_eq, controller_1_beq,
       controller_1_blez, controller_1_bne, controller_1_j, controller_1_jal, controller_1_jr,
       controller_1_memtoreg, controller_1_memwrite, controller_1_regwrite, controller_1_sh,
       controller_1_syscall, correct_b, ex_mem_1_halt_2, ex_mem_1_jal_2, ex_mem_1_sh_2, halt, halt_1_halt,
       id_ex_1_jal_2, id_ex_1_sh_2, IR1, IR2, IR3, j, j_bub, j_jal_2_out, j_jal_out, jal, jmp, jr, loaduse,
       LOCK, mem_2_out, mem_3_out, mem_4_out, mem_out, memtoreg, MemToReg_M, MemToReg_WB, memwrite,
       MemWrite_M, nor_2_out, nor_out, not_1_out, not_2_out, not_3_out, not_4_out, not_5_out, not_6_out,
       not_7_out, not_8_out, not_9_out, not_10_out, not_11_out, not_12_out, not_13_out, not_14_out,
       not_15_out, not_16_out, not_17_out, not_18_out, not_19_out, not_20_out, not_21_out, not_22_out,
       not_23_out, not_24_out, not_25_out, not_26_out, not_27_out, not_28_out, not_29_out, or_3_out,
       or_4_out, or_6_out, or_7_out, or_8_out, or_9_out, or_10_out, or_11_out, or_12_out, or_13_out,
       or_14_out, or_15_out, or_out, RegDst, register_1_q, register_2_q, register_3_q, RST, slt_2_out,
       slt_out, sltu_2_out, sltu_out, sub_2_out, sub_out, sw_2_out, sw_3_out, sw_4_out, sw_out, Syscall,
       syscall_2_out, syscall_out, W1, W2, W3, WB, WB_2_out, WB_3_out, WB_4_out, WB_out, WE, WE_EX;
  wire [1:0] controller_1_extop;
  wire [3:0] controller_1_aluop, id_ex_1_aluop_2;
  wire [4:0] decoder_1__10_6, decoder_1__15_11, decoder_1__20_16, decoder_1__25_21, multiplexer_2_out,
       multiplexer_3_out, multiplexer_4_out, multiplexer_5_out, multiplexer_6_out, RA, RB, Rd, Rd_EX, RW;
  wire [5:0] func, func1, op, op1;
  wire [15:0] decoder_1__15_0, \load_use次数 , \总周期数 , \插入气泡数 , \无条件分支指令数 , \有条件分支成功跳转 , \有条件分支指令数 ;
  wire [31:0] A, A_f, adder_1_out, alu_1_p5, B, B_f, decoder_1_index, ex_mem_1_b_2, ex_mem_1_pc_4_2,
       ex_mem_1_r_2, extender_1_out_4, id_ex_1_ext_2, id_ex_1_index_2, id_ex_1_pc_4_2, if_id_1_pc_4_2,
       \if_id_1_指令_2 , mem_wb_1_d_2, mem_wb_1_pc_4_2, mem_wb_1_r_2, multiplexer_1_out, multiplexer_7_out,
       multiplexer_8_out, multiplexer_12_out, multiplexer_13_out, multiplexer_16_out, npc_1_out_13, PC_q,
       ram_1_data, registerfile_1_p7, registerfile_1_p8, rom_1_data, SyscallOut, w_MEM, w_RB;

  Button \u_总复位  (.out(RST));
  Button _1 (.out(IR1));
  Button _2 (.out(IR2));
  Button _3 (.out(IR3));
  Clock clock_1 (.out(CLK));
  LED led_1 (.in(W1));
  LED led_2 (.in(W2));
  LED led_3 (.in(W3));
  DISP disp_1 (.RF_A(A_f), .Syscall(Syscall), .clk(CLK), .RF_B(B_f), .rst(RST), .Syscallout(SyscallOut));
  not not_1 (not_1_out, loaduse);
  and and_1 (and_1_out, not_1_out, not_2_out);
  not not_2 (not_2_out, LOCK);
  Hex_Digit_Display hex_digit_display_1 (.value(SyscallOut[31:28]));  // open: dp
  Multiplexer #(.width(32), .enable("false")) multiplexer_1 (
    .in0(adder_1_out), .in1(npc_1_out_13), .out(multiplexer_1_out), .sel(j_bub));
  // Probe on Rd
  // Probe on Rd
  // Probe on RW
  Comparator #(.width(6), .mode("unsigned")) comparator_1 (
    .a(op), .b({6{1'b0}}), .eq(comparator_1_eq));  // open: gt, lt
  Comparator #(.width(6), .mode("unsigned")) comparator_2 (
    .a(func), .b(6'b100000), .eq(comparator_2_eq));  // open: gt, lt
  Comparator #(.width(6), .mode("unsigned")) comparator_3 (
    .a(op), .b({6{1'b0}}), .eq(comparator_3_eq));  // open: gt, lt
  Comparator #(.width(6), .mode("unsigned")) comparator_4 (
    .a(func), .b(6'b100001), .eq(comparator_4_eq));  // open: gt, lt
  Comparator #(.width(6), .mode("unsigned")) comparator_5 (
    .a(op), .b({6{1'b0}}), .eq(comparator_5_eq));  // open: gt, lt
  Comparator #(.width(6), .mode("unsigned")) comparator_6 (
    .a(func), .b(6'b100100), .eq(comparator_6_eq));  // open: gt, lt
  Comparator #(.width(6), .mode("unsigned")) comparator_7 (
    .a(op), .b({6{1'b0}}), .eq(comparator_7_eq));  // open: gt, lt
  Comparator #(.width(6), .mode("unsigned")) comparator_8 (
    .a(func), .b(6'b100010), .eq(comparator_8_eq));  // open: gt, lt
  Comparator #(.width(6), .mode("unsigned")) comparator_9 (
    .a(op), .b({6{1'b0}}), .eq(comparator_9_eq));  // open: gt, lt
  Comparator #(.width(6), .mode("unsigned")) comparator_10 (
    .a(func), .b(6'b100101), .eq(comparator_10_eq));  // open: gt, lt
  Comparator #(.width(6), .mode("unsigned")) comparator_11 (
    .a(op), .b({6{1'b0}}), .eq(comparator_11_eq));  // open: gt, lt
  Comparator #(.width(6), .mode("unsigned")) comparator_12 (
    .a(func), .b(6'b100111), .eq(comparator_12_eq));  // open: gt, lt
  Comparator #(.width(6), .mode("unsigned")) comparator_13 (
    .a(op), .b(6'b101011), .eq(comparator_13_eq));  // open: gt, lt
  Comparator #(.width(6), .mode("unsigned")) comparator_14 (
    .a(op), .b(6'b000100), .eq(comparator_14_eq));  // open: gt, lt
  Comparator #(.width(6), .mode("unsigned")) comparator_15 (
    .a(op), .b(6'b000101), .eq(comparator_15_eq));  // open: gt, lt
  Comparator #(.width(6), .mode("unsigned")) comparator_16 (
    .a(op), .b({6{1'b0}}), .eq(comparator_16_eq));  // open: gt, lt
  Comparator #(.width(6), .mode("unsigned")) comparator_17 (
    .a(func), .b(6'b101010), .eq(comparator_17_eq));  // open: gt, lt
  Comparator #(.width(6), .mode("unsigned")) comparator_18 (
    .a(op), .b({6{1'b0}}), .eq(comparator_18_eq));  // open: gt, lt
  Comparator #(.width(6), .mode("unsigned")) comparator_19 (
    .a(func), .b(6'b101011), .eq(comparator_19_eq));  // open: gt, lt
  Comparator #(.width(6), .mode("unsigned")) comparator_20 (
    .a(op), .b({6{1'b0}}), .eq(comparator_20_eq));  // open: gt, lt
  Comparator #(.width(6), .mode("unsigned")) comparator_21 (
    .a(func), .b(6'b001100), .eq(comparator_21_eq));  // open: gt, lt
  Hex_Digit_Display hex_digit_display_2 (.value(SyscallOut[27:24]));  // open: dp
  Hex_Digit_Display hex_digit_display_3 (.value(SyscallOut[23:20]));  // open: dp
  Register #(.width(32)) PC (.D(multiplexer_1_out), .en(and_1_out), .Q(PC_q), .clk(CLK), .clr(RST));
  // Probe on RW
  // Probe on RB
  Hex_Digit_Display hex_digit_display_4 (.value(SyscallOut[19:16]));  // open: dp
  Hex_Digit_Display hex_digit_display_5 (.value(SyscallOut[15:12]));  // open: dp
  not not_3 (not_3_out, loaduse);
  Comparator #(.width(5), .mode("unsigned")) comparator_22 (
    .a({5{1'b0}}), .b(Rd), .eq(comparator_22_eq));  // open: gt, lt
  Comparator #(.width(5), .mode("unsigned")) comparator_23 (.a(Rd), .b(RA), .eq(comparator_23_eq));  // open: gt, lt
  Comparator #(.width(5), .mode("unsigned")) comparator_24 (
    .a({5{1'b0}}), .b(RW), .eq(comparator_24_eq));  // open: gt, lt
  Comparator #(.width(5), .mode("unsigned")) comparator_25 (.a(RW), .b(RA), .eq(comparator_25_eq));  // open: gt, lt
  // Probe on RA
  Comparator #(.width(5), .mode("unsigned")) comparator_26 (
    .a({5{1'b0}}), .b(Rd), .eq(comparator_26_eq));  // open: gt, lt
  Comparator #(.width(5), .mode("unsigned")) comparator_27 (.a(Rd), .b(RB), .eq(comparator_27_eq));  // open: gt, lt
  Comparator #(.width(5), .mode("unsigned")) comparator_28 (
    .a({5{1'b0}}), .b(RW), .eq(comparator_28_eq));  // open: gt, lt
  Comparator #(.width(5), .mode("unsigned")) comparator_29 (.a(RW), .b(RB), .eq(comparator_29_eq));  // open: gt, lt
  and add (add_out, comparator_1_eq, comparator_2_eq);
  and addu (addu_out, comparator_3_eq, comparator_4_eq);
  and and_2 (and_2_out, comparator_5_eq, comparator_6_eq);
  and sub (sub_out, comparator_7_eq, comparator_8_eq);
  and \or  (or_out, comparator_9_eq, comparator_10_eq);
  and \nor  (nor_out, comparator_11_eq, comparator_12_eq);
  and sw (sw_out, comparator_13_eq, 1'b1);
  and u_beq (beq_out, comparator_14_eq, 1'b1);
  and u_bne (bne_out, comparator_15_eq, 1'b1);
  and slt (slt_out, comparator_16_eq, comparator_17_eq);
  and sltu (sltu_out, comparator_18_eq, comparator_19_eq);
  and u_syscall (syscall_out, comparator_20_eq, comparator_21_eq);
  Hex_Digit_Display hex_digit_display_6 (.value(SyscallOut[7:4]));  // open: dp
  Hex_Digit_Display hex_digit_display_7 (.value(SyscallOut[11:8]));  // open: dp
  // Probe on adder_1_out
  Adder #(.width(32)) adder_1 (.a(32'h1), .b(PC_q), .out(adder_1_out));  // open: cin, cout
  ROM #(.addrWidth(10), .dataWidth(32)) rom_1 (.addr(PC_q[9:0]), .data(rom_1_data));  // open: sel
  and and_3 (and_3_out, not_3_out, not_2_out);
  or or_2 (bub1, j_bub, RST);
  not not_4 (not_4_out, comparator_22_eq);
  not not_5 (not_5_out, comparator_23_eq);
  not not_6 (not_6_out, comparator_24_eq);
  Comparator #(.width(6), .mode("unsigned")) comparator_30 (
    .a(op), .b(6'b000010), .eq(comparator_30_eq));  // open: gt, lt
  Comparator #(.width(6), .mode("unsigned")) comparator_31 (
    .a(op), .b(6'b000011), .eq(comparator_31_eq));  // open: gt, lt
  Comparator #(.width(6), .mode("unsigned")) comparator_32 (
    .a(op), .b(6'b101011), .eq(comparator_32_eq));  // open: gt, lt
  not not_7 (not_7_out, comparator_26_eq);
  not not_8 (not_8_out, comparator_27_eq);
  not not_9 (not_9_out, comparator_28_eq);
  Hex_Digit_Display hex_digit_display_8 (.value(SyscallOut[3:0]));  // open: dp
  IF_ID if_id_1 (
    .PC_4(adder_1_out), .\指令 (rom_1_data), .in_3(bub1), .in_4(CLK), .PC_4_2(if_id_1_pc_4_2),
    .\指令_2 (\if_id_1_指令_2 ), .Lock(and_3_out));
  decoder decoder_1 (
    .index(decoder_1_index), .in_1(\if_id_1_指令_2 ), .op_31_26(op1), ._25_21(decoder_1__25_21),
    ._20_16(decoder_1__20_16), .func_5_0(func1), ._10_6(decoder_1__10_6), ._15_11(decoder_1__15_11),
    ._15_0(decoder_1__15_0));
  or j_jal (j_jal_out, comparator_30_eq, comparator_31_eq);
  and sw_2 (sw_2_out, comparator_32_eq, 1'b1);
  // Probe on if_id_1_pc_4_2
  controller controller_1 (
    .func(func1), .op(op1), .RegDst(RegDst), .ALUsrc(alusrc1), .blez(controller_1_blez),
    .MemWrite(controller_1_memwrite), .RegWrite(controller_1_regwrite), .ALUOP(controller_1_aluop),
    .MemToReg(controller_1_memtoreg), .EXTOP(controller_1_extop), .beq(controller_1_beq),
    .bne(controller_1_bne), .j(controller_1_j), .jal(controller_1_jal), .jr(controller_1_jr),
    .Syscall(controller_1_syscall), .sh(controller_1_sh));
  // Probe on op1
  and mem (mem_out, not_4_out, comparator_23_eq, WE);
  and u_WB (WB_out, not_5_out, not_6_out, comparator_25_eq, WB);
  not not_10 (not_10_out, j_jal_out);
  not not_11 (not_11_out, ALUSrc);
  and mem_2 (mem_2_out, not_7_out, comparator_27_eq, WE);
  and WB_2 (WB_2_out, not_8_out, not_9_out, comparator_29_eq, WB);
  or or_3 (or_3_out, add_out, addu_out, and_2_out, sub_out, or_out, nor_out, sw_out, beq_out, bne_out, slt_out, sltu_out, syscall_out);
  // Probe on \总周期数 
  // Probe on \无条件分支指令数 
  // Probe on \有条件分支指令数 
  // Probe on \有条件分支成功跳转 
  // Probe on \load_use次数 
  Comparator #(.width(2), .mode("unsigned")) comparator_33 (
    .a(controller_1_extop), .b(2'b10), .eq(comparator_33_eq));  // open: gt, lt
  // Probe on controller_1_extop
  extender extender_1 (
    .in_1(decoder_1__15_0), .in_3(decoder_1__10_6), .out_4(extender_1_out_4), .in_2(controller_1_extop));
  or or_4 (or_4_out, sw_2_out, not_11_out);
  and and_4 (B_MEM, mem_2_out, or_4_out, or_3_out);
  and and_5 (B_WB, or_3_out, or_4_out, WB_2_out);
  Multiplexer #(.width(5), .enable("false")) multiplexer_2 (
    .in0(decoder_1__25_21), .in1(decoder_1__20_16), .out(multiplexer_2_out), .sel(comparator_33_eq));
  Multiplexer #(.width(5), .enable("false")) multiplexer_3 (
    .in0(multiplexer_2_out), .in1(5'b00010), .out(multiplexer_3_out), .sel(controller_1_syscall));
  Multiplexer #(.width(5), .enable("false")) multiplexer_4 (
    .in0(decoder_1__20_16), .in1(decoder_1__15_11), .out(multiplexer_4_out), .sel(RegDst));
  and and_6 (A_MEM, mem_out, not_10_out);
  and and_7 (A_WB, not_10_out, WB_out);
  Multiplexer #(.width(5), .enable("false")) multiplexer_5 (
    .in0(decoder_1__20_16), .in1(5'b00100), .out(multiplexer_5_out), .sel(controller_1_syscall));
  Multiplexer #(.width(5), .enable("false")) multiplexer_6 (
    .in0(multiplexer_4_out), .in1({5{1'b1}}), .out(multiplexer_6_out), .sel(controller_1_jal));
  not not_12 (not_12_out, halt);
  // Probe on multiplexer_3_out
  Counter #(.width(16), .max('hffff)) counter_1 (
    .D(16'h1), .Q(\总周期数 ), .clk(and_8_out), .clr(RST));  // open: load, count, carry
  and and_8 (and_8_out, register_1_q, CLK);
  Register #(.width(1)) register_1 (.D(not_12_out), .Q(register_1_q), .clk(CLK), .clr(RST));  // open: en
  // RegisterFile registerfile_1: pin names not known; wires that end beside it: w_RB, CLK, WB, RW, multiplexer_3_out, multiplexer_5_out, registerfile_1_p7, registerfile_1_p8
  // Probe on multiplexer_5_out
  ID_EX id_ex_1 (
    .PC_4(if_id_1_pc_4_2), .in_1(bub2), .in_2(CLK), .PC_4_2(id_ex_1_pc_4_2), .ALUsrc_2(ALUSrc),
    .MemToReg_2(memtoreg), .MemWrite_2(memwrite), .blez_2(blez), .beq_2(beq), .bne_2(bne), .j_2(j),
    .jal_2(id_ex_1_jal_2), .jr_2(jr), .ALUOP_2(id_ex_1_aluop_2), .ALUsrc(alusrc1),
    .MemToReg(controller_1_memtoreg), .MemWrite(controller_1_memwrite), .blez(controller_1_blez),
    .beq(controller_1_beq), .bne(controller_1_bne), .j(controller_1_j), .jal(controller_1_jal),
    .jr(controller_1_jr), .ALUOP(controller_1_aluop), .sh(controller_1_sh), .sh_2(id_ex_1_sh_2),
    .A(registerfile_1_p7), .A_2(A), .B(registerfile_1_p8), .B_2(B), .EXT(extender_1_out_4),
    .EXT_2(id_ex_1_ext_2), .INDEX(decoder_1_index), .INDEX_2(id_ex_1_index_2),
    .RegWrite(controller_1_regwrite), .RegWrite_2(WE_EX), .RW(multiplexer_6_out), .RW_2(Rd_EX),
    .syscall(controller_1_syscall), .syscall_2(Syscall), .LOCK(not_2_out), .RA(multiplexer_3_out), .RA_2(RA),
    .RB(multiplexer_5_out), .RB_2(RB), .op(op1), .op_2(op), .func(func1), .func_2(func));
  or or_5 (bub2, loaduse, j_bub, RST);
  and and_9 (and_9_out, or_6_out, not_13_out);
  or or_6 (or_6_out, blez, beq, bne);
  // Probe on RB
  Counter #(.width(16), .max('hffff)) counter_2 (
    .D(16'h1), .Q(\有条件分支指令数 ), .clk(and_9_out), .clr(RST));  // open: load, count, carry
  not not_13 (not_13_out, CLK);
  halt halt_1 (.RF_A(A_f), .syscall(Syscall), .halt(halt_1_halt), .rst(RST));
  // Probe on A_f
  Multiplexer #(.width(32), .enable("false")) multiplexer_7 (
    .in0(B_f), .in1(id_ex_1_ext_2), .out(multiplexer_7_out), .sel(ALUSrc));
  // ALU alu_1: pin names not known; wires that end beside it: A_f, multiplexer_7_out, id_ex_1_aluop_2, alu_1_p4, alu_1_p5
  npc npc_1 (
    .\是否相等 (alu_1_p4), .RF_A(A_f), .PC_1(id_ex_1_pc_4_2), .ext(id_ex_1_ext_2), .correct_b(correct_b),
    .beq(beq), .bne(bne), .blez(blez), .index(id_ex_1_index_2), .jr(jr), .j(j), .jal(id_ex_1_jal_2),
    .out_13(npc_1_out_13), .jmp(jmp));
  // Probe on npc_1_out_13
  Multiplexer #(.width(32), .enable("false")) multiplexer_8 (
    .in0(A), .in1(w_MEM), .out(multiplexer_8_out), .sel(A_MEM));
  // Probe on w_MEM
  Counter #(.width(16), .max('hffff)) counter_3 (
    .D(16'h1), .Q(\有条件分支成功跳转 ), .clk(and_10_out), .clr(RST));  // open: load, count, carry
  and and_10 (and_10_out, correct_b, not_14_out);
  Multiplexer #(.enable("false")) multiplexer_9 (.in0(register_2_q), .in1(1'b1), .out(LOCK), .sel(halt));
  // Probe on alu_1_p5
  // Probe on alu_1_p5
  not not_14 (not_14_out, CLK);
  EX_MEM ex_mem_1 (
    .in_1(RST), .in_2(CLK), .PC_4(id_ex_1_pc_4_2), .MemToReg(memtoreg), .MemWrite(memwrite), .R(alu_1_p5),
    .jal(id_ex_1_jal_2), .B(B_f), .sh(id_ex_1_sh_2), .PC_4_2(ex_mem_1_pc_4_2), .MemToReg_2(MemToReg_M),
    .MemWrite_2(MemWrite_M), .R_2(ex_mem_1_r_2), .jal_2(ex_mem_1_jal_2), .B_2(ex_mem_1_b_2),
    .sh_2(ex_mem_1_sh_2), .RegWrite(WE_EX), .RegWrite_2(WE), .RW(Rd_EX), .RW_2(Rd), .halt(halt_1_halt),
    .halt_2(ex_mem_1_halt_2), .LOCK(not_2_out));  // open: NPC, NPC_2
  // Probe on ex_mem_1_r_2
  // Probe on ex_mem_1_b_2
  // Probe on A_f
  Multiplexer #(.width(32), .enable("false")) multiplexer_10 (
    .in0(multiplexer_8_out), .in1(w_RB), .out(A_f), .sel(A_WB));
  Register #(.width(1)) register_2 (.D(LOCK), .Q(register_2_q), .clk(CLK), .clr(RST));  // open: en
  // Probe on ex_mem_1_pc_4_2
  Multiplexer #(.width(32), .enable("false")) multiplexer_11 (
    .in0(ex_mem_1_r_2), .in1(ex_mem_1_pc_4_2), .out(w_MEM), .sel(ex_mem_1_jal_2));
  Multiplexer #(.width(32), .enable("false")) multiplexer_12 (
    .in0(ex_mem_1_b_2), .in1({{16{1'b0}}, ex_mem_1_b_2[15:0]}), .out(multiplexer_12_out), .sel(ex_mem_1_sh_2));
  or or_7 (or_7_out, jmp, correct_b);
  not not_15 (not_15_out, or_7_out);
  not not_16 (not_16_out, register_3_q);
  Counter #(.width(16), .max('hffff)) counter_4 (
    .D(16'h1), .Q(\无条件分支指令数 ), .clk(and_11_out), .clr(RST));  // open: load, count, carry
  and and_11 (and_11_out, or_8_out, not_17_out);
  or or_8 (or_8_out, j, jal, jr);
  // Probe on Rd
  // Probe on ex_mem_1_r_2[11:0]
  Multiplexer #(.width(32), .enable("false")) multiplexer_13 (
    .in0(B), .in1(w_MEM), .out(multiplexer_13_out), .sel(B_MEM));
  Multiplexer #(.enable("false")) multiplexer_14 (.in0(not_16_out), .in1(1'b0), .out(j_bub), .sel(not_15_out));
  not not_17 (not_17_out, CLK);
  Register #(.width(1)) register_3 (.D(j_bub), .Q(register_3_q), .clk(CLK), .clr(RST));  // open: en
  MEM_WB mem_wb_1 (
    .in_1(RST), .in_2(CLK), .PC_4(ex_mem_1_pc_4_2), .MemToReg(MemToReg_M), .R(ex_mem_1_r_2),
    .jal(ex_mem_1_jal_2), .D(ram_1_data), .PC_4_2(mem_wb_1_pc_4_2), .MemToReg_2(MemToReg_WB),
    .R_2(mem_wb_1_r_2), .jal_2(jal), .D_2(mem_wb_1_d_2), .RegWrite(WE), .RegWrite_2(WB), .RW(Rd), .RW_2(RW),
    .halt(ex_mem_1_halt_2), .halt_2(halt), .LOCK(not_2_out));
  RAM #(.addrWidth(12), .dataWidth(32), .bus("separate")) ram_1 (
    .addr(ex_mem_1_r_2[11:0]), .din(multiplexer_12_out), .data(ram_1_data), .str(MemWrite_M), .clk(CLK),
    .ld(MemToReg_M), .clr(RST));  // open: sel
  // Probe on B_f
  Multiplexer #(.width(32), .enable("false")) multiplexer_15 (
    .in0(multiplexer_13_out), .in1(w_RB), .out(B_f), .sel(B_WB));
  // Probe on mem_wb_1_pc_4_2
  // Probe on w_RB
  Counter #(.width(16), .max('hffff)) counter_5 (
    .D(16'h1), .Q(\插入气泡数 ), .clk(and_12_out), .clr(RST));  // open: load, count, carry
  and and_12 (and_12_out, and_13_out, not_18_out);
  not not_18 (not_18_out, CLK);
  and and_13 (and_13_out, bub2, not_21_out);
  Counter #(.width(16), .max('hffff)) counter_6 (
    .D(16'h1), .Q(\load_use次数 ), .clk(and_14_out), .clr(RST));  // open: load, count, carry
  and and_14 (and_14_out, and_15_out, not_19_out);
  not not_19 (not_19_out, CLK);
  and and_15 (and_15_out, loaduse, not_20_out);
  not not_20 (not_20_out, halt);
  Multiplexer #(.width(32), .enable("false")) multiplexer_16 (
    .in0(mem_wb_1_r_2), .in1(mem_wb_1_d_2), .out(multiplexer_16_out), .sel(MemToReg_WB));
  Multiplexer #(.width(32), .enable("false")) multiplexer_17 (
    .in0(multiplexer_16_out), .in1(mem_wb_1_pc_4_2), .out(w_RB), .sel(jal));
  not not_21 (not_21_out, halt);
  // Probe on RW
  // Probe on Rd
  // Probe on Rd
  // Probe on Rd_EX
  Comparator #(.width(6), .mode("unsigned")) comparator_34 (
    .a(op1), .b({6{1'b0}}), .eq(comparator_34_eq));  // open: gt, lt
  Comparator #(.width(6), .mode("unsigned")) comparator_35 (
    .a(func1), .b(6'b100000), .eq(comparator_35_eq));  // open: gt, lt
  Comparator #(.width(6), .mode("unsigned")) comparator_36 (
    .a(op1), .b({6{1'b0}}), .eq(comparator_36_eq));  // open: gt, lt
  Comparator #(.width(6), .mode("unsigned")) comparator_37 (
    .a(func1), .b(6'b100001), .eq(comparator_37_eq));  // open: gt, lt
  Comparator #(.width(6), .mode("unsigned")) comparator_38 (
    .a(op1), .b({6{1'b0}}), .eq(comparator_38_eq));  // open: gt, lt
  Comparator #(.width(6), .mode("unsigned")) comparator_39 (
    .a(func1), .b(6'b100100), .eq(comparator_39_eq));  // open: gt, lt
  Comparator #(.width(6), .mode("unsigned")) comparator_40 (
    .a(op1), .b({6{1'b0}}), .eq(comparator_40_eq));  // open: gt, lt
  Comparator #(.width(6), .mode("unsigned")) comparator_41 (
    .a(func1), .b(6'b100010), .eq(comparator_41_eq));  // open: gt, lt
  Comparator #(.width(6), .mode("unsigned")) comparator_42 (
    .a(op1), .b({6{1'b0}}), .eq(comparator_42_eq));  // open: gt, lt
  Comparator #(.width(6), .mode("unsigned")) comparator_43 (
    .a(func1), .b(6'b100101), .eq(comparator_43_eq));  // open: gt, lt
  Comparator #(.width(6), .mode("unsigned")) comparator_44 (
    .a(op1), .b({6{1'b0}}), .eq(comparator_44_eq));  // open: gt, lt
  Comparator #(.width(6), .mode("unsigned")) comparator_45 (
    .a(func1), .b(6'b100111), .eq(comparator_45_eq));  // open: gt, lt
  Comparator #(.width(6), .mode("unsigned")) comparator_46 (
    .a(op1), .b(6'b101011), .eq(comparator_46_eq));  // open: gt, lt
  Comparator #(.width(6), .mode("unsigned")) comparator_47 (
    .a(op1), .b(6'b000100), .eq(comparator_47_eq));  // open: gt, lt
  Comparator #(.width(6), .mode("unsigned")) comparator_48 (
    .a(op1), .b(6'b000101), .eq(comparator_48_eq));  // open: gt, lt
  Comparator #(.width(6), .mode("unsigned")) comparator_49 (
    .a(op1), .b({6{1'b0}}), .eq(comparator_49_eq));  // open: gt, lt
  Comparator #(.width(6), .mode("unsigned")) comparator_50 (
    .a(func1), .b(6'b101010), .eq(comparator_50_eq));  // open: gt, lt
  Comparator #(.width(6), .mode("unsigned")) comparator_51 (
    .a(op1), .b({6{1'b0}}), .eq(comparator_51_eq));  // open: gt, lt
  Comparator #(.width(6), .mode("unsigned")) comparator_52 (
    .a(func1), .b(6'b101011), .eq(comparator_52_eq));  // open: gt, lt
  Comparator #(.width(6), .mode("unsigned")) comparator_53 (
    .a(op1), .b({6{1'b0}}), .eq(comparator_53_eq));  // open: gt, lt
  Comparator #(.width(6), .mode("unsigned")) comparator_54 (
    .a(func1), .b(6'b001100), .eq(comparator_54_eq));  // open: gt, lt
  // Probe on Rd_EX
  Comparator #(.width(5), .mode("unsigned")) comparator_55 (
    .a({5{1'b0}}), .b(Rd), .eq(comparator_55_eq));  // open: gt, lt
  Comparator #(.width(5), .mode("unsigned")) comparator_56 (.a(Rd), .b(RA), .eq(comparator_56_eq));  // open: gt, lt
  Comparator #(.width(5), .mode("unsigned")) comparator_57 (
    .a({5{1'b0}}), .b(Rd_EX), .eq(comparator_57_eq));  // open: gt, lt
  Comparator #(.width(5), .mode("unsigned")) comparator_58 (.a(Rd_EX), .b(RA), .eq(comparator_58_eq));  // open: gt, lt
  // Probe on RA
  Comparator #(.width(5), .mode("unsigned")) comparator_59 (
    .a({5{1'b0}}), .b(Rd), .eq(comparator_59_eq));  // open: gt, lt
  Comparator #(.width(5), .mode("unsigned")) comparator_60 (.a(Rd), .b(RB), .eq(comparator_60_eq));  // open: gt, lt
  Comparator #(.width(5), .mode("unsigned")) comparator_61 (
    .a({5{1'b0}}), .b(Rd_EX), .eq(comparator_61_eq));  // open: gt, lt
  Comparator #(.width(5), .mode("unsigned")) comparator_62 (.a(Rd_EX), .b(RB), .eq(comparator_62_eq));  // open: gt, lt
  // Probe on RB
  and add_2 (add_2_out, comparator_34_eq, comparator_35_eq);
  and addu_2 (addu_2_out, comparator_36_eq, comparator_37_eq);
  and and_16 (and_16_out, comparator_38_eq, comparator_39_eq);
  and sub_2 (sub_2_out, comparator_40_eq, comparator_41_eq);
  and or_9 (or_9_out, comparator_42_eq, comparator_43_eq);
  and nor_2 (nor_2_out, comparator_44_eq, comparator_45_eq);
  and sw_3 (sw_3_out, comparator_46_eq, 1'b1);
  and beq_2 (beq_2_out, comparator_47_eq, 1'b1);
  and bne_2 (bne_2_out, comparator_48_eq, 1'b1);
  and slt_2 (slt_2_out, comparator_49_eq, comparator_50_eq);
  and sltu_2 (sltu_2_out, comparator_51_eq, comparator_52_eq);
  and syscall_2 (syscall_2_out, comparator_53_eq, comparator_54_eq);
  not not_22 (not_22_out, comparator_55_eq);
  not not_23 (not_23_out, comparator_56_eq);
  not not_24 (not_24_out, comparator_57_eq);
  Comparator #(.width(6), .mode("unsigned")) comparator_63 (
    .a(op1), .b(6'b000010), .eq(comparator_63_eq));  // open: gt, lt
  Comparator #(.width(6), .mode("unsigned")) comparator_64 (
    .a(op1), .b(6'b000011), .eq(comparator_64_eq));  // open: gt, lt
  Comparator #(.width(6), .mode("unsigned")) comparator_65 (
    .a(op1), .b(6'b101011), .eq(comparator_65_eq));  // open: gt, lt
  not not_25 (not_25_out, comparator_59_eq);
  not not_26 (not_26_out, comparator_60_eq);
  not not_27 (not_27_out, comparator_61_eq);
  and sw_4 (sw_4_out, comparator_65_eq, 1'b1);
  and mem_3 (mem_3_out, not_22_out, comparator_56_eq, WE);
  and WB_3 (WB_3_out, not_23_out, not_24_out, comparator_58_eq, WE_EX);
  not not_28 (not_28_out, j_jal_2_out);
  or j_jal_2 (j_jal_2_out, comparator_63_eq, comparator_64_eq);
  not not_29 (not_29_out, alusrc1);
  and mem_4 (mem_4_out, not_25_out, comparator_60_eq, WE);
  and WB_4 (WB_4_out, not_26_out, not_27_out, comparator_62_eq, WE_EX);
  or or_10 (or_10_out, add_2_out, addu_2_out, and_16_out, sub_2_out, or_9_out, nor_2_out, sw_3_out, beq_2_out, bne_2_out, slt_2_out, sltu_2_out, syscall_2_out);
  or or_11 (or_11_out, sw_4_out, not_29_out);
  and and_17 (and_17_out, mem_3_out, not_28_out);
  and and_18 (and_18_out, not_28_out, WB_3_out);
  and and_19 (and_19_out, mem_4_out, or_11_out, or_10_out);
  and and_20 (and_20_out, or_10_out, or_11_out, WB_4_out);
  or or_12 (or_12_out, MemToReg_M, MemWrite_M);
  or or_13 (or_13_out, and_17_out, and_19_out);
  or or_14 (or_14_out, and_18_out, and_20_out);
  and and_21 (and_21_out, or_12_out, or_13_out);
  or or_15 (or_15_out, memtoreg, memwrite);
  and and_22 (and_22_out, or_15_out, or_14_out);
  or or_16 (loaduse, and_21_out, and_22_out);

  // Other names for the same wires on the sheet: MemWrite_WB = MemToReg_WB; RF_A[31:0] = A_f

  // Notes on the sheet:
  //   指令存储器
  //   contents of rom_1 (hex, n*v repeats v):
  //   20110001 8000c05 20110001 20120002 20130003 8000c09 20110001 20120002 20130003 8000c0d 20110001
  //   20120002 20130003 8000c11 20110001 20120002 20130003 c000cb8 20100001 20110001 118fc0 112020
  //   20020022 c 118882 12200001 8000c15 112020 20020022 c 20110001 118880 112020 20020022 c 12200001
  //   8000c1f 20110001 118fc0 112020 20020022 c 1188c3 112020 20020022 c 118903 112020 20020022 c 118903
  //   112020 20020022 c 118903 112020 20020022 c 118903 112020 20020022 c 118903 112020 20020022 c 118903
  //   112020 20020022 c 118903 112020 20020022 c 20100001 109fc0 139fc3 8021 2012000c 24160003 26100001
  //   3210000f 20080008 20090001 139900 2709825 132020 20020022 c 1094022 1500fff9 22100001 2018000f
  //   2188024 108700 20080008 20090001 139902 2709825 132021 20020022 c 1094022 1500fff9 108702 2c9b022
  //   12c00001 8000c50 4020 1084027 84400 3508ffff 82021 20020022 c 2010ffff 20110000 ae300000 22100001
  //   22310004 ae300000 22100001 22310004 ae300000 22100001 22310004 ae300000 22100001 22310004 ae300000
  //   22100001 22310004 ae300000 22100001 22310004 ae300000 22100001 22310004 ae300000 22100001 22310004
  //   ae300000 22100001 22310004 ae300000 22100001 22310004 ae300000 22100001 22310004 ae300000 22100001
  //   22310004 ae300000 22100001 22310004 ae300000 22100001 22310004 ae300000 22100001 22310004 ae300000
  //   22100001 22310004 22100001 8020 2011003c 8e130000 8e340000 274402a 11000002 ae330000 ae140000
  //   2231fffc 1611fff8 102020 20020022 c 22100004 2011003c 1611fff2 2002000a c 20100000 22100001 102020
  //   20020022 c 22100002 102020 20020022 c 22100003 102020 20020022 c 22100004 102020 20020022 c 22100005
  //   102020 20020022 c 22100006 102020 20020022 c 22100007 102020 20020022 c 22100008 102020 20020022
  //   20020022 c 3e00008
  //   数码管输出
  //   译码器
  //   控制器
  //   [25:21]
  //   [20:16]
  //   15:11
  //   位扩展
  //   前一条指令的memtoreg过memwrite为1时，代表是仿存指令，在发生冲突即load-use
  //   数据存储器
endmodule

module controller (
  input  [5:0] func,
  input  [5:0] op,
  output RegDst,
  output ALUsrc,
  output RegWrite,
  output MemToReg,
  output MemWrite,
  output [1:0] EXTOP,
  output blez,
  output beq,
  output bne,
  output j,
  output jal,
  output jr,
  output Syscall,
  output [3:0] ALUOP,
  output sh
);

  wire add, add_out, addi_out, addiu_out, addu_out, \and , and_out, andi_out, \nor , not_1_out, not_2_out,
       not_3_out, not_4_out, not_5_out, not_6_out, not_7_out, not_8_out, not_9_out, not_10_out, not_11_out,
       not_12_out, not_13_out, not_14_out, not_15_out, not_16_out, not_17_out, not_18_out, not_19_out,
       not_20_out, not_21_out, not_22_out, not_23_out, \or , or_out, sll, slt, slt_out, slti_out, sltiu_out,
       sltu, sltu_out, sra, srl, sub, sw_out, \xor ;

  not not_1 (not_1_out, func[5]);
  not not_2 (not_2_out, func[4]);
  not not_3 (not_3_out, func[3]);
  not not_4 (not_4_out, func[1]);
  not not_5 (not_5_out, func[2]);
  not not_6 (not_6_out, func[0]);
  not not_7 (not_7_out, op[5]);
  not not_8 (not_8_out, op[4]);
  not not_9 (not_9_out, op[3]);
  not not_10 (not_10_out, op[2]);
  not not_11 (not_11_out, op[0]);
  not not_12 (not_12_out, op[1]);
  and u_add (add_out, not_7_out, not_8_out, not_9_out, not_10_out, not_12_out, not_11_out, func[5], not_2_out, not_3_out, not_5_out, not_4_out, not_6_out);
  and addi (addi_out, not_7_out, not_8_out, op[3], not_10_out, not_12_out, not_11_out);
  and addiu (addiu_out, not_7_out, not_8_out, op[3], not_10_out, not_12_out, op[0]);
  and addu (addu_out, not_7_out, not_8_out, not_9_out, not_10_out, not_12_out, not_11_out, func[5], not_2_out, not_3_out, not_5_out, not_4_out, func[0]);
  and u_and (and_out, not_7_out, not_8_out, not_9_out, not_10_out, not_12_out, not_11_out, func[5], not_2_out, not_3_out, func[2], not_4_out, not_6_out);
  and andi (andi_out, not_7_out, not_8_out, op[3], op[2], not_12_out, not_11_out);
  and u_sll (sll, not_7_out, not_8_out, not_9_out, not_10_out, not_12_out, not_11_out, not_1_out, not_2_out, not_3_out, not_5_out, not_4_out, not_6_out);
  and u_sra (sra, not_7_out, not_8_out, not_9_out, not_10_out, not_12_out, not_11_out, not_1_out, not_2_out, not_3_out, not_5_out, func[1], func[0]);
  and u_srl (srl, not_7_out, not_8_out, not_9_out, not_10_out, not_12_out, not_11_out, not_1_out, not_2_out, not_3_out, not_5_out, func[1], not_6_out);
  and u_sub (sub, not_7_out, not_8_out, not_9_out, not_10_out, not_12_out, not_11_out, func[5], not_2_out, not_3_out, not_5_out, func[1], not_6_out);
  and u_or (or_out, not_7_out, not_8_out, not_9_out, not_10_out, not_12_out, not_11_out, func[5], not_2_out, not_3_out, func[2], not_4_out, func[0]);
  and ori (EXTOP[0], not_7_out, not_8_out, op[3], op[2], not_12_out, op[0]);
  and u_nor (\nor , not_7_out, not_8_out, not_9_out, not_10_out, not_12_out, not_11_out, func[5], not_2_out, not_3_out, func[2], func[1], func[0]);
  and lw (MemToReg, op[5], not_8_out, not_9_out, not_10_out, op[1], op[0]);
  and sw (sw_out, op[5], not_8_out, op[3], not_10_out, op[1], op[0]);
  and u_beq (beq, not_7_out, not_8_out, not_9_out, op[2], not_12_out, not_11_out);
  and u_bne (bne, not_7_out, not_8_out, not_9_out, op[2], not_12_out, op[0]);
  and u_slt (slt_out, not_7_out, not_8_out, not_9_out, not_10_out, not_12_out, not_11_out, func[5], not_2_out, func[3], not_5_out, func[1], not_6_out);
  and slti (slti_out, not_7_out, not_8_out, op[3], not_10_out, op[1], not_11_out);
  and u_sltu (sltu_out, not_7_out, not_8_out, not_9_out, not_10_out, not_12_out, not_11_out, func[5], not_2_out, func[3], not_5_out, func[1], func[0]);
  and u_j (j, not_7_out, not_8_out, not_9_out, not_10_out, op[1], not_11_out);
  and u_jal (jal, not_7_out, not_8_out, not_9_out, not_10_out, op[1], op[0]);
  and u_jr (jr, not_7_out, not_8_out, not_9_out, not_10_out, not_12_out, not_11_out, not_1_out, not_2_out, func[3], not_5_out, not_4_out, not_6_out);
  and u_syscall (Syscall, not_7_out, not_8_out, not_9_out, not_10_out, not_12_out, not_11_out, not_1_out, not_2_out, func[3], func[2], not_4_out, not_6_out);
  and u_xor (\xor , not_7_out, not_8_out, not_9_out, not_10_out, not_12_out, not_11_out, func[5], not_2_out, not_3_out, func[2], func[1], not_6_out);
  and sltiu (sltiu_out, not_7_out, not_8_out, op[3], not_10_out, op[1], op[0]);
  and u_sh (sh, op[5], not_8_out, op[3], not_10_out, not_12_out, op[0]);
  and u_blez (blez, not_7_out, not_8_out, not_9_out, op[2], op[1], not_11_out);
  or or_2 (RegDst, add_out, addu_out, and_out, sll, sra, srl, sub, or_out, \nor , slt_out, sltu_out, \xor );
  or or_3 (ALUsrc, addi_out, addiu_out, andi_out, sll, sra, srl, EXTOP[0], MemToReg, sw_out, slti_out, sltiu_out, sh);
  or or_4 (RegWrite, add_out, addi_out, addiu_out, addu_out, and_out, andi_out, sll, sra, srl, sub, or_out, EXTOP[0], \nor , MemToReg, slt_out, slti_out, sltu_out, jal, \xor , sltiu_out);
  or or_5 (MemWrite, sw_out, sh);
  or or_6 (EXTOP[1], sll, sra, srl);
  or and_2 (\and , and_out, andi_out);
  or or_7 (\or , or_out, EXTOP[0]);
  or slt_2 (slt, slt_out, slti_out);
  or ALUOP3 (ALUOP[3], \or , \xor , \nor , slt, sltu);
  or ALUOP2 (ALUOP[2], add, sub, \and , sltu);
  or ALUOP1 (ALUOP[1], srl, sub, \and , \nor , slt);
  or ALUOP0 (ALUOP[0], sra, add, \and , \xor , slt);
  or sltu_2 (sltu, sltu_out, sltiu_out);
  not not_13 (not_13_out, sll);
  not not_14 (not_14_out, sra);
  or add_2 (add, add_out, addi_out, addiu_out, addu_out, MemToReg, sw_out, sh);
  not not_15 (not_15_out, add);
  not not_16 (not_16_out, srl);
  not not_17 (not_17_out, \and );
  not not_18 (not_18_out, sub);
  not not_19 (not_19_out, \or );
  not not_20 (not_20_out, \xor );
  not not_21 (not_21_out, slt);
  not not_22 (not_22_out, \nor );
  not not_23 (not_23_out, sltu);
endmodule

module decoder (
  input  [31:0] in_1,
  output [31:0] index,
  output [5:0] op_31_26,
  output [4:0] _25_21,
  output [4:0] _20_16,
  output [15:0] _15_0,
  output [5:0] func_5_0,
  output [4:0] _10_6,
  output [4:0] _15_11
);


  assign _10_6 = in_1[10:6];
  assign _15_0 = in_1[15:0];
  assign _15_11 = in_1[15:11];
  assign _20_16 = in_1[20:16];
  assign _25_21 = in_1[25:21];
  assign func_5_0 = in_1[5:0];
  assign index = {{6{1'b0}}, in_1[25:0]};
  assign op_31_26 = in_1[31:26];

  // Notes on the sheet:
  //   指令
endmodule

module extender (
  input  [15:0] in_1,
  input  [1:0] in_2,
  input  [4:0] in_3,
  output [31:0] out_4
);

  wire [31:0] bit_extender_1_out, bit_extender_2_out, bit_extender_3_out;

  assign bit_extender_1_out = {{16{in_1[15]}}, in_1};  // Bit_Extender bit_extender_1
  assign bit_extender_2_out = {{16{1'b0}}, in_1};  // Bit_Extender bit_extender_2
  assign bit_extender_3_out = {{27{1'b0}}, in_3};  // Bit_Extender bit_extender_3
  Multiplexer #(.select(2), .width(32), .enable("false")) multiplexer_1 (
    .in0(bit_extender_1_out), .in1(bit_extender_2_out), .in2(bit_extender_3_out), .in3({32{1'b0}}),
    .out(out_4), .sel(in_2));

  // Notes on the sheet:
  //   [15:0]
  //   [10:6]
endmodule

module npc (
  input  \是否相等 ,
  input  [31:0] RF_A,
  input  beq,
  input  bne,
  input  [31:0] PC_1,
  input  blez,
  input  [31:0] ext,
  input  j,
  input  jal,
  input  [31:0] index,
  input  jr,
  output correct_b,
  output [31:0] out_13,
  output jmp
);

  wire and_1_out, and_2_out, and_3_out, comparator_1_gt, not_1_out, not_2_out, or_2_out;
  wire [31:0] adder_1_out, multiplexer_2_out, multiplexer_3_out;

  Multiplexer #(.width(32), .enable("false")) multiplexer_1 (
    .in0(multiplexer_2_out), .in1(RF_A), .out(out_13), .sel(jr));
  Adder #(.width(32)) adder_1 (.a(PC_1), .b(ext), .out(adder_1_out));  // open: cin, cout
  Multiplexer #(.width(32), .enable("false")) multiplexer_2 (
    .in0(multiplexer_3_out), .in1(index), .out(multiplexer_2_out), .sel(or_2_out));
  or or_1 (correct_b, and_1_out, and_2_out, and_3_out);
  Multiplexer #(.width(32), .enable("false")) multiplexer_3 (
    .in0(PC_1), .in1(adder_1_out), .out(multiplexer_3_out), .sel(correct_b));
  or or_2 (or_2_out, j, jal);
  or or_3 (jmp, j, jr, jal);
  and and_1 (and_1_out, \是否相等 , beq);
  and and_2 (and_2_out, not_1_out, bne);
  not not_1 (not_1_out, \是否相等 );
  and and_3 (and_3_out, not_2_out, blez);
  not not_2 (not_2_out, comparator_1_gt);
  Comparator #(.width(32), .mode("unsigned")) comparator_1 (
    .a(RF_A), .b({32{1'b0}}), .gt(comparator_1_gt));  // open: eq, lt
endmodule

module halt (
  input  [31:0] RF_A,
  input  syscall,
  input  rst,
  output halt
);

  wire and_1_out, comparator_1_eq, not_1_out;

  Comparator #(.width(32)) comparator_1 (.a(RF_A), .b(32'ha), .eq(comparator_1_eq));  // open: gt, lt
  and and_1 (and_1_out, comparator_1_eq, syscall);
  not not_1 (not_1_out, halt);
  Register #(.width(1)) register_1 (.D(not_1_out), .Q(halt), .clk(and_1_out), .clr(rst));  // open: en
endmodule

module DISP (
  input  [31:0] RF_A,
  input  Syscall,
  input  clk,
  input  rst,
  input  [31:0] RF_B,
  output [31:0] Syscallout
);

  wire and_1_out, comparator_1_eq, not_1_out;
  wire [31:0] multiplexer_1_out, register_1_q;

  Comparator #(.width(32), .mode("unsigned")) comparator_1 (.a(RF_A), .b(32'ha), .eq(comparator_1_eq));  // open: gt, lt
  not not_1 (not_1_out, comparator_1_eq);
  and and_1 (and_1_out, not_1_out, Syscall);
  Multiplexer #(.width(32), .enable("false")) multiplexer_1 (
    .in0(register_1_q), .in1(RF_B), .out(multiplexer_1_out), .sel(and_1_out));
  Register #(.width(32)) register_1 (.D(multiplexer_1_out), .en(1'b1), .Q(register_1_q), .clk(clk), .clr(rst));
  Multiplexer #(.width(32), .enable("false")) multiplexer_2 (
    .in0(register_1_q), .in1(multiplexer_1_out), .out(Syscallout), .sel(and_1_out));
endmodule

module IF_ID (
  input  [31:0] PC_4,
  input  [31:0] \指令 ,
  input  in_3,
  input  in_4,
  input  Lock,
  output [31:0] PC_4_2,
  output [31:0] \指令_2 
);

  wire [31:0] multiplexer_1_out, multiplexer_2_out;

  Multiplexer #(.width(32), .enable("false")) multiplexer_1 (
    .in0(PC_4), .in1({32{1'b0}}), .out(multiplexer_1_out), .sel(in_3));
  Multiplexer #(.width(32), .enable("false")) multiplexer_2 (
    .in0(\指令 ), .in1({32{1'b0}}), .out(multiplexer_2_out), .sel(in_3));
  Register #(.width(32)) register_1 (.D(multiplexer_1_out), .en(Lock), .Q(PC_4_2), .clk(in_4));  // open: clr
  Register #(.width(32)) register_2 (.D(multiplexer_2_out), .en(Lock), .Q(\指令_2 ), .clk(in_4));  // open: clr

  // Other names for the same wires on the sheet: CLK = in_4; RST = in_3
endmodule

module ID_EX (
  input  in_1,
  input  in_2,
  input  [31:0] PC_4,
  input  RegWrite,
  input  ALUsrc,
  input  [31:0] A,
  input  MemToReg,
  input  [31:0] B,
  input  MemWrite,
  input  blez,
  input  [31:0] EXT,
  input  beq,
  input  [31:0] INDEX,
  input  bne,
  input  [4:0] RW,
  input  j,
  input  [4:0] RA,
  input  jal,
  input  [4:0] RB,
  input  jr,
  input  [5:0] op,
  input  syscall,
  input  [3:0] ALUOP,
  input  [5:0] func,
  input  sh,
  input  LOCK,
  output [31:0] PC_4_2,
  output RegWrite_2,
  output ALUsrc_2,
  output [31:0] A_2,
  output MemToReg_2,
  output [31:0] B_2,
  output MemWrite_2,
  output blez_2,
  output [31:0] EXT_2,
  output beq_2,
  output [31:0] INDEX_2,
  output bne_2,
  output [4:0] RW_2,
  output j_2,
  output [4:0] RA_2,
  output jal_2,
  output [4:0] RB_2,
  output jr_2,
  output [5:0] op_2,
  output syscall_2,
  output [3:0] ALUOP_2,
  output [5:0] func_2,
  output sh_2
);

  wire multiplexer_2_out, multiplexer_3_out, multiplexer_4_out, multiplexer_5_out, multiplexer_6_out,
       multiplexer_7_out, multiplexer_8_out, multiplexer_9_out, multiplexer_10_out, multiplexer_11_out,
       multiplexer_13_out, multiplexer_14_out;
  wire [3:0] multiplexer_12_out;
  wire [4:0] multiplexer_19_out, multiplexer_20_out, multiplexer_21_out;
  wire [5:0] multiplexer_22_out, multiplexer_23_out;
  wire [31:0] multiplexer_1_out, multiplexer_15_out, multiplexer_16_out, multiplexer_17_out,
       multiplexer_18_out;

  Multiplexer #(.width(32), .enable("false")) multiplexer_1 (
    .in0(PC_4), .in1({32{1'b0}}), .out(multiplexer_1_out), .sel(in_1));
  Multiplexer #(.enable("false")) multiplexer_2 (.in0(ALUsrc), .in1(1'b0), .out(multiplexer_2_out), .sel(in_1));
  Multiplexer #(.enable("false")) multiplexer_3 (.in0(MemToReg), .in1(1'b0), .out(multiplexer_3_out), .sel(in_1));
  Multiplexer #(.enable("false")) multiplexer_4 (.in0(MemWrite), .in1(1'b0), .out(multiplexer_4_out), .sel(in_1));
  Multiplexer #(.enable("false")) multiplexer_5 (.in0(blez), .in1(1'b0), .out(multiplexer_5_out), .sel(in_1));
  Multiplexer #(.enable("false")) multiplexer_6 (.in0(beq), .in1(1'b0), .out(multiplexer_6_out), .sel(in_1));
  Multiplexer #(.enable("false")) multiplexer_7 (.in0(bne), .in1(1'b0), .out(multiplexer_7_out), .sel(in_1));
  Multiplexer #(.enable("false")) multiplexer_8 (.in0(j), .in1(1'b0), .out(multiplexer_8_out), .sel(in_1));
  Multiplexer #(.enable("false")) multiplexer_9 (.in0(jal), .in1(1'b0), .out(multiplexer_9_out), .sel(in_1));
  Multiplexer #(.enable("false")) multiplexer_10 (.in0(jr), .in1(1'b0), .out(multiplexer_10_out), .sel(in_1));
  Multiplexer #(.enable("false")) multiplexer_11 (.in0(syscall), .in1(1'b0), .out(multiplexer_11_out), .sel(in_1));
  Multiplexer #(.width(4), .enable("false")) multiplexer_12 (
    .in0(ALUOP), .in1(4'b0000), .out(multiplexer_12_out), .sel(in_1));
  Multiplexer #(.enable("false")) multiplexer_13 (.in0(sh), .in1(1'b0), .out(multiplexer_13_out), .sel(in_1));
  Register #(.width(32)) register_1 (.D(multiplexer_1_out), .en(LOCK), .Q(PC_4_2), .clk(in_2));  // open: clr
  Register #(.width(1)) register_2 (.D(multiplexer_2_out), .en(LOCK), .Q(ALUsrc_2), .clk(in_2));  // open: clr
  Register #(.width(1)) register_3 (.D(multiplexer_3_out), .en(LOCK), .Q(MemToReg_2), .clk(in_2));  // open: clr
  Register #(.width(1)) register_4 (.D(multiplexer_4_out), .en(LOCK), .Q(MemWrite_2), .clk(in_2));  // open: clr
  Register #(.width(1)) register_5 (.D(multiplexer_5_out), .en(LOCK), .Q(blez_2), .clk(in_2));  // open: clr
  Register #(.width(1)) register_6 (.D(multiplexer_6_out), .en(LOCK), .Q(beq_2), .clk(in_2));  // open: clr
  Register #(.width(1)) register_7 (.D(multiplexer_7_out), .en(LOCK), .Q(bne_2), .clk(in_2));  // open: clr
  Register #(.width(1)) register_8 (.D(multiplexer_8_out), .en(LOCK), .Q(j_2), .clk(in_2));  // open: clr
  Register #(.width(1)) register_9 (.D(multiplexer_9_out), .en(LOCK), .Q(jal_2), .clk(in_2));  // open: clr
  Register #(.width(1)) register_10 (.D(multiplexer_10_out), .en(LOCK), .Q(jr_2), .clk(in_2));  // open: clr
  Register #(.width(1)) register_11 (.D(multiplexer_11_out), .en(LOCK), .Q(syscall_2), .clk(in_2));  // open: clr
  Register #(.width(4)) register_12 (.D(multiplexer_12_out), .en(LOCK), .Q(ALUOP_2), .clk(in_2));  // open: clr
  Register #(.width(1)) register_13 (.D(multiplexer_13_out), .en(LOCK), .Q(sh_2), .clk(in_2));  // open: clr
  Multiplexer #(.enable("false")) multiplexer_14 (.in0(RegWrite), .in1(1'b0), .out(multiplexer_14_out), .sel(in_1));
  Multiplexer #(.width(32), .enable("false")) multiplexer_15 (
    .in0(A), .in1({32{1'b0}}), .out(multiplexer_15_out), .sel(in_1));
  Multiplexer #(.width(32), .enable("false")) multiplexer_16 (
    .in0(B), .in1({32{1'b0}}), .out(multiplexer_16_out), .sel(in_1));
  Multiplexer #(.width(32), .enable("false")) multiplexer_17 (
    .in0(EXT), .in1({32{1'b0}}), .out(multiplexer_17_out), .sel(in_1));
  Multiplexer #(.width(32), .enable("false")) multiplexer_18 (
    .in0(INDEX), .in1({32{1'b0}}), .out(multiplexer_18_out), .sel(in_1));
  Multiplexer #(.width(5), .enable("false")) multiplexer_19 (
    .in0(RW), .in1({5{1'b0}}), .out(multiplexer_19_out), .sel(in_1));
  Multiplexer #(.width(5), .enable("false")) multiplexer_20 (
    .in0(RA), .in1({5{1'b0}}), .out(multiplexer_20_out), .sel(in_1));
  Multiplexer #(.width(5), .enable("false")) multiplexer_21 (
    .in0(RB), .in1({5{1'b0}}), .out(multiplexer_21_out), .sel(in_1));
  Multiplexer #(.width(6), .enable("false")) multiplexer_22 (
    .in0(op), .in1({6{1'b0}}), .out(multiplexer_22_out), .sel(in_1));
  Multiplexer #(.width(6), .enable("false")) multiplexer_23 (
    .in0(func), .in1({6{1'b0}}), .out(multiplexer_23_out), .sel(in_1));
  Register #(.width(1)) register_14 (.D(multiplexer_14_out), .en(LOCK), .Q(RegWrite_2), .clk(in_2));  // open: clr
  Register #(.width(32)) register_15 (.D(multiplexer_15_out), .en(LOCK), .Q(A_2), .clk(in_2));  // open: clr
  Register #(.width(32)) register_16 (.D(multiplexer_16_out), .en(LOCK), .Q(B_2), .clk(in_2));  // open: clr
  Register #(.width(32)) register_17 (.D(multiplexer_17_out), .en(LOCK), .Q(EXT_2), .clk(in_2));  // open: clr
  Register #(.width(32)) register_18 (.D(multiplexer_18_out), .en(LOCK), .Q(INDEX_2), .clk(in_2));  // open: clr
  Register #(.width(5)) register_19 (.D(multiplexer_19_out), .en(LOCK), .Q(RW_2), .clk(in_2));  // open: clr
  Register #(.width(5)) register_20 (.D(multiplexer_20_out), .en(LOCK), .Q(RA_2), .clk(in_2));  // open: clr
  Register #(.width(5)) register_21 (.D(multiplexer_21_out), .en(LOCK), .Q(RB_2), .clk(in_2));  // open: clr
  Register #(.width(6)) register_22 (.D(multiplexer_22_out), .en(LOCK), .Q(op_2), .clk(in_2));  // open: clr
  Register #(.width(6)) register_23 (.D(multiplexer_23_out), .en(LOCK), .Q(func_2), .clk(in_2));  // open: clr

  // Other names for the same wires on the sheet: CLK = in_2; RF_A[31:0] = A; RST = in_1
endmodule

module EX_MEM (
  input  in_1,
  input  in_2,
  input  [31:0] PC_4,
  input  RegWrite,
  input  MemToReg,
  input  [31:0] R,
  input  MemWrite,
  input  [31:0] B,
  input  jal,
  input  [31:0] NPC,
  input  sh,
  input  [4:0] RW,
  input  halt,
  input  LOCK,
  output [31:0] PC_4_2,
  output RegWrite_2,
  output MemToReg_2,
  output [31:0] R_2,
  output MemWrite_2,
  output [31:0] B_2,
  output jal_2,
  output [31:0] NPC_2,
  output sh_2,
  output [4:0] RW_2,
  output halt_2
);

  wire multiplexer_2_out, multiplexer_3_out, multiplexer_4_out, multiplexer_5_out, multiplexer_6_out,
       multiplexer_7_out;
  wire [4:0] multiplexer_11_out;
  wire [31:0] multiplexer_1_out, multiplexer_8_out, multiplexer_9_out, multiplexer_10_out;

  Multiplexer #(.width(32), .enable("false")) multiplexer_1 (
    .in0(PC_4), .in1({32{1'b0}}), .out(multiplexer_1_out), .sel(in_1));
  Multiplexer #(.enable("false")) multiplexer_2 (.in0(MemToReg), .in1(1'b0), .out(multiplexer_2_out), .sel(in_1));
  Multiplexer #(.enable("false")) multiplexer_3 (.in0(MemWrite), .in1(1'b0), .out(multiplexer_3_out), .sel(in_1));
  Multiplexer #(.enable("false")) multiplexer_4 (.in0(jal), .in1(1'b0), .out(multiplexer_4_out), .sel(in_1));
  Multiplexer #(.enable("false")) multiplexer_5 (.in0(sh), .in1(1'b0), .out(multiplexer_5_out), .sel(in_1));
  Multiplexer #(.enable("false")) multiplexer_6 (.in0(halt), .in1(1'b0), .out(multiplexer_6_out), .sel(in_1));
  Register #(.width(32)) register_1 (.D(multiplexer_1_out), .en(LOCK), .Q(PC_4_2), .clk(in_2));  // open: clr
  Register #(.width(1)) register_2 (.D(multiplexer_2_out), .en(LOCK), .Q(MemToReg_2), .clk(in_2));  // open: clr
  Register #(.width(1)) register_3 (.D(multiplexer_3_out), .en(LOCK), .Q(MemWrite_2), .clk(in_2));  // open: clr
  Register #(.width(1)) register_4 (.D(multiplexer_4_out), .en(LOCK), .Q(jal_2), .clk(in_2));  // open: clr
  Register #(.width(1)) register_5 (.D(multiplexer_5_out), .en(LOCK), .Q(sh_2), .clk(in_2));  // open: clr
  Register #(.width(1)) register_6 (.D(multiplexer_6_out), .en(LOCK), .Q(halt_2), .clk(in_2));  // open: clr
  Multiplexer #(.enable("false")) multiplexer_7 (.in0(RegWrite), .in1(1'b0), .out(multiplexer_7_out), .sel(in_1));
  Multiplexer #(.width(32), .enable("false")) multiplexer_8 (
    .in0(R), .in1({32{1'b0}}), .out(multiplexer_8_out), .sel(in_1));
  Multiplexer #(.width(32), .enable("false")) multiplexer_9 (
    .in0(B), .in1({32{1'b0}}), .out(multiplexer_9_out), .sel(in_1));
  Multiplexer #(.width(32), .enable("false")) multiplexer_10 (
    .in0(NPC), .in1({32{1'b0}}), .out(multiplexer_10_out), .sel(in_1));
  Multiplexer #(.width(5), .enable("false")) multiplexer_11 (
    .in0(RW), .in1({5{1'b0}}), .out(multiplexer_11_out), .sel(in_1));
  Register #(.width(1)) register_7 (.D(multiplexer_7_out), .en(LOCK), .Q(RegWrite_2), .clk(in_2));  // open: clr
  Register #(.width(32)) register_8 (.D(multiplexer_8_out), .en(LOCK), .Q(R_2), .clk(in_2));  // open: clr
  Register #(.width(32)) register_9 (.D(multiplexer_9_out), .en(LOCK), .Q(B_2), .clk(in_2));  // open: clr
  Register #(.width(32)) register_10 (.D(multiplexer_10_out), .en(LOCK), .Q(NPC_2), .clk(in_2));  // open: clr
  Register #(.width(5)) register_11 (.D(multiplexer_11_out), .en(LOCK), .Q(RW_2), .clk(in_2));  // open: clr

  // Other names for the same wires on the sheet: CLK = in_2; RST = in_1
endmodule

module MEM_WB (
  input  in_1,
  input  in_2,
  input  [31:0] PC_4,
  input  RegWrite,
  input  MemToReg,
  input  [31:0] R,
  input  jal,
  input  [31:0] D,
  input  [4:0] RW,
  input  halt,
  input  LOCK,
  output [31:0] PC_4_2,
  output RegWrite_2,
  output MemToReg_2,
  output [31:0] R_2,
  output jal_2,
  output [31:0] D_2,
  output [4:0] RW_2,
  output halt_2
);

  wire multiplexer_2_out, multiplexer_3_out, multiplexer_5_out, multiplexer_7_out, register_1_q;
  wire [4:0] multiplexer_4_out;
  wire [31:0] multiplexer_1_out, multiplexer_8_out, multiplexer_9_out;

  Multiplexer #(.width(32), .enable("false")) multiplexer_1 (
    .in0(PC_4), .in1({32{1'b0}}), .out(multiplexer_1_out), .sel(in_1));
  Multiplexer #(.enable("false")) multiplexer_2 (.in0(MemToReg), .in1(1'b0), .out(multiplexer_2_out), .sel(in_1));
  Multiplexer #(.enable("false")) multiplexer_3 (.in0(jal), .in1(1'b0), .out(multiplexer_3_out), .sel(in_1));
  Multiplexer #(.width(5), .enable("false")) multiplexer_4 (
    .in0(RW), .in1({5{1'b0}}), .out(multiplexer_4_out), .sel(in_1));
  Multiplexer #(.enable("false")) multiplexer_5 (.in0(halt), .in1(1'b0), .out(multiplexer_5_out), .sel(in_1));
  Register #(.width(1)) register_1 (.D(multiplexer_5_out), .en(LOCK), .Q(register_1_q), .clk(in_2));  // open: clr
  Register #(.width(32)) register_2 (.D(multiplexer_1_out), .en(LOCK), .Q(PC_4_2), .clk(in_2));  // open: clr
  Register #(.width(1)) register_3 (.D(multiplexer_2_out), .en(LOCK), .Q(MemToReg_2), .clk(in_2));  // open: clr
  Register #(.width(1)) register_4 (.D(multiplexer_3_out), .en(LOCK), .Q(jal_2), .clk(in_2));  // open: clr
  Register #(.width(5)) register_5 (.D(multiplexer_4_out), .en(LOCK), .Q(RW_2), .clk(in_2));  // open: clr
  Multiplexer #(.enable("false")) multiplexer_6 (.in0(register_1_q), .in1(1'b0), .out(halt_2), .sel(in_1));
  Multiplexer #(.enable("false")) multiplexer_7 (.in0(RegWrite), .in1(1'b0), .out(multiplexer_7_out), .sel(in_1));
  Multiplexer #(.width(32), .enable("false")) multiplexer_8 (
    .in0(R), .in1({32{1'b0}}), .out(multiplexer_8_out), .sel(in_1));
  Multiplexer #(.width(32), .enable("false")) multiplexer_9 (
    .in0(D), .in1({32{1'b0}}), .out(multiplexer_9_out), .sel(in_1));
  Register #(.width(1)) register_6 (.D(multiplexer_7_out), .en(LOCK), .Q(RegWrite_2), .clk(in_2));  // open: clr
  Register #(.width(32)) register_7 (.D(multiplexer_8_out), .en(LOCK), .Q(R_2), .clk(in_2));  // open: clr
  Register #(.width(32)) register_8 (.D(multiplexer_9_out), .en(LOCK), .Q(D_2), .clk(in_2));  // open: clr

  // Other names for the same wires on the sheet: CLK = in_2; RST = in_1
endmodule
