// Logisim project CS1503_U201514559_周铭昊_CPU.circ as structural Verilog: 2 circuits, main circuit cpu
module cpu (
);

  wire _3break2, alu_1_p4, ALUsrc, and_1_out, and_2_out, and_3_out, and_4_out, and_5_out, and_6_out,
       and_7_out, and_8_out, and_9_out, and_10_out, and_11_out, and_12_out, and_13_out, and_14_out,
       and_18_out, and_20_out, and_21_out, and_22_out, and_23_out, and_24_out, and_25_out, and_26_out,
       and_27_out, and_28_out, and_29_out, and_30_out, beq, blez, bne, \break , break2, CLK, comparator_1_eq,
       comparator_2_eq, comparator_3_gt, comparator_4_eq, comparator_5_gt, comparator_6_gt, comparator_8_eq,
       comparator_9_eq, comparator_10_eq, comparator_11_eq, comparator_12_lt, comparator_13_gt,
       comparator_14_eq, comparator_15_eq, correct_b, d_ff_1_q, d_ff_2_q, d_ff_3_q, d_ff_4_q, d_ff_5_q,
       \EPC入栈 , \EPC出栈 , eret, halt, IE, IG1, IG2, IG3, IR1, IR1_S, IR2, IR2_S, IR3, IR3_S, j, jal, jr,
       MemToReg, Memwrite, mfc0, mtc0, nor_1_out, not_1_out, not_2_out, not_3_out, not_4_out, not_5_out,
       not_6_out, not_7_out, not_8_out, not_9_out, not_11_out, not_12_out, not_13_out, not_14_out,
       not_15_out, not_16_out, not_17_out, or_4_out, or_6_out, or_7_out, or_8_out, or_12_out, or_13_out,
       or_14_out, or_15_out, or_16_out, or_17_out, or_18_out, or_19_out, or_22_out, or_23_out, RegDst,
       register_1_q, register_2_q, register_3_q, register_4_q, RegWrite, RST, S, s_r_ff_1_q, sh, Syscall, W1,
       W2, W3, w11, w22, w111, w222, w1111, w2222;
  wire [1:0] EXTOP, \当前中断 ;
  wire [2:0] IR;
  wire [3:0] ALUOP;
  wire [4:0] _20_16, multiplexer_2_out, multiplexer_3_out, multiplexer_4_out, multiplexer_7_out,
       multiplexer_8_out;
  wire [15:0] \总周期数 , \无条件分支指令数 , \有条件分支成功跳转 , \有条件分支指令数 ;
  wire [25:0] index;
  wire [31:0] adder_1_out, adder_2_out, alu_1_p5, bit_extender_1_out, bit_extender_2_out, bit_extender_3_out,
       breakaddr, DM, EPC, multiplexer_1_out, multiplexer_5_out, multiplexer_6_out, multiplexer_9_out,
       multiplexer_10_out, multiplexer_11_out, multiplexer_13_out, multiplexer_14_out, multiplexer_15_out,
       multiplexer_16_out, multiplexer_17_out, multiplexer_18_out, multiplexer_19_out, pc, register_6_q,
       registerfile_1_p8, RF_A, SyscallOut;
  wire [31:26] rom_1_data;

  Button \u_总复位  (.out(RST));
  Clock clock_1 (.out(CLK));
  Button _1 (.out(IR1));
  Button _2 (.out(IR2));
  Button _3 (.out(IR3));
  nor nor_1 (nor_1_out, halt, \break );
  LED _1_2 (.in(W1));
  LED _2_2 (.in(W2));
  LED _3_2 (.in(W3));
  // Probe on pc
  Register #(.width(32)) u_PC (.D(multiplexer_1_out), .en(nor_1_out), .Q(pc), .clk(CLK), .clr(RST));
  Comparator #(.width(32)) comparator_1 (.a(RF_A), .b(32'ha), .eq(comparator_1_eq));  // open: gt, lt
  and and_1 (and_1_out, IG3, \break );
  and and_2 (and_2_out, IG2, \break );
  Comparator #(.width(2), .mode("unsigned")) comparator_2 (
    .a(\当前中断 ), .b(2'b01), .eq(comparator_2_eq));  // open: gt, lt
  Hex_Digit_Display hex_digit_display_1 (.value(SyscallOut[31:28]));  // open: dp
  Hex_Digit_Display hex_digit_display_2 (.value(SyscallOut[27:24]));  // open: dp
  Adder #(.width(32)) adder_1 (.a(32'h1), .b(pc), .out(adder_1_out));  // open: cin, cout
  ROM #(.addrWidth(10), .dataWidth(32)) rom_1 (
    .addr(pc[9:0]), .data({rom_1_data, index[25:21], _20_16, index[15:0]}));  // open: sel
  or or_1 (w11, IR1_S, d_ff_1_q);
  or or_2 (w22, IR2_S, d_ff_2_q);
  or or_3 (W3, IR3_S, d_ff_3_q);
  or or_4 (or_4_out, and_1_out, and_2_out);
  Hex_Digit_Display hex_digit_display_3 (.value(SyscallOut[19:16]));  // open: dp
  Hex_Digit_Display hex_digit_display_4 (.value(SyscallOut[23:20]));  // open: dp
  and and_3 (and_3_out, comparator_1_eq, Syscall);
  D_Flip_Flop d_ff_1 (.clk(IR1), .D(1'b1), .Q(d_ff_1_q), .reset(IR1_S));  // open: Qn, preset, en
  and and_4 (and_4_out, IG1, \break );
  D_Flip_Flop d_ff_2 (.clk(IR2), .D(1'b1), .Q(d_ff_2_q), .reset(IR2_S));  // open: Qn, preset, en
  and and_5 (and_5_out, IG2, \break );
  D_Flip_Flop d_ff_3 (.clk(IR3), .D(1'b1), .Q(d_ff_3_q), .reset(IR3_S));  // open: Qn, preset, en
  and and_6 (and_6_out, IG3, \break );
  and and_7 (and_7_out, or_4_out, comparator_2_eq);
  Hex_Digit_Display hex_digit_display_5 (.value(SyscallOut[15:12]));  // open: dp
  Hex_Digit_Display hex_digit_display_6 (.value(SyscallOut[11:8]));  // open: dp
  // Probe on multiplexer_1_out
  // Probe on rom_1_data
  // Probe on index[5:0]
  buf or_5 (halt, and_3_out);  // OR_Gate
  or or_6 (or_6_out, d_ff_1_q, IR1_S);
  Register #(.width(1)) register_1 (.D(and_4_out), .Q(register_1_q), .clk(CLK), .clr(RST));  // open: en
  or or_7 (or_7_out, d_ff_2_q, IR2_S);
  Register #(.width(1)) register_2 (.D(and_5_out), .Q(register_2_q), .clk(CLK), .clr(RST));  // open: en
  or or_8 (or_8_out, d_ff_3_q, IR3_S);
  Register #(.width(1)) register_3 (.D(and_6_out), .Q(register_3_q), .clk(CLK), .clr(RST));  // open: en
  or or_9 (w111, w1111, d_ff_4_q);
  Comparator #(.width(2), .mode("unsigned")) comparator_3 (
    .a(\当前中断 ), .b(2'b10), .gt(comparator_3_gt));  // open: eq, lt
  Comparator #(.width(2), .mode("unsigned")) comparator_4 (
    .a(\当前中断 ), .b(2'b11), .eq(comparator_4_eq));  // open: gt, lt
  not not_1 (not_1_out, W2);
  Hex_Digit_Display hex_digit_display_7 (.value(SyscallOut[3:0]));  // open: dp
  Hex_Digit_Display hex_digit_display_8 (.value(SyscallOut[7:4]));  // open: dp
  and and_8 (and_8_out, or_6_out, ~register_1_q);  // AND_Gate
  and and_9 (and_9_out, or_7_out, ~register_2_q);  // AND_Gate
  and and_10 (and_10_out, or_8_out, ~register_3_q);  // AND_Gate
  D_Flip_Flop d_ff_4 (.clk(and_7_out), .D(1'b1), .Q(d_ff_4_q), .reset(w1111));  // open: Qn, preset, en
  not not_2 (not_2_out, comparator_3_gt);
  and and_11 (and_11_out, not_2_out, \EPC出栈 );
  and and_12 (and_12_out, comparator_4_eq, \EPC出栈 , not_1_out);
  D_Flip_Flop u_IR1 (.clk(CLK), .D(and_8_out), .Q(IR1_S));  // open: Qn, preset, en, reset
  D_Flip_Flop IR1_2 (.clk(CLK), .D(and_9_out), .Q(IR2_S));  // open: Qn, preset, en, reset
  D_Flip_Flop IR1_3 (.clk(CLK), .D(and_10_out), .Q(IR3_S));  // open: Qn, preset, en, reset
  or or_10 (W1, w11, w111);
  or or_11 (W2, w22, w222);
  or or_12 (or_12_out, d_ff_4_q, w1111);
  and and_13 (and_13_out, or_12_out, ~or_13_out);  // AND_Gate
  or or_13 (or_13_out, and_11_out, and_12_out);
  Multiplexer #(.width(32), .enable("false")) multiplexer_1 (
    .in0(multiplexer_5_out), .in1(EPC), .out(multiplexer_1_out), .sel(eret));
  controller controller_1 (
    .func(index[5:0]), .op(rom_1_data), .RegDst(RegDst), .ALUsrc(ALUsrc), .blez(blez), .MemWrite(Memwrite),
    .RegWrite(RegWrite), .ALUOP(ALUOP), .MemToReg(MemToReg), .EXTOP(EXTOP), .beq(beq), .bne(bne), .j(j),
    .jal(jal), .jr(jr), .Syscall(Syscall), .sh(sh), ._25_21(index[25:21]), .mfc0(mfc0), .mtc0(mtc0),
    .eret(eret));
  D_Flip_Flop IR1_4 (.clk(CLK), .D(and_13_out), .Q(w1111));  // open: Qn, preset, en, reset
  // Probe on \总周期数 
  // Probe on \无条件分支指令数 
  // Probe on \有条件分支指令数 
  // Probe on \有条件分支成功跳转 
  Multiplexer #(.width(5), .enable("false")) multiplexer_2 (
    .in0(index[25:21]), .in1(_20_16), .out(multiplexer_2_out), .sel(S));
  Multiplexer #(.width(5), .enable("false")) multiplexer_3 (
    .in0(_20_16), .in1(index[15:11]), .out(multiplexer_3_out), .sel(RegDst));
  Multiplexer #(.width(5), .enable("false")) multiplexer_4 (
    .in0(multiplexer_2_out), .in1(5'b00010), .out(multiplexer_4_out), .sel(Syscall));
  assign bit_extender_1_out = {{16{index[15]}}, index[15:0]};  // Bit_Extender bit_extender_1
  assign bit_extender_2_out = {{16{1'b0}}, index[15:0]};  // Bit_Extender bit_extender_2
  assign bit_extender_3_out = {{27{1'b0}}, index[10:6]};  // Bit_Extender bit_extender_3
  Comparator #(.width(2), .mode("unsigned")) comparator_5 (
    .a(\当前中断 ), .b(2'b01), .gt(comparator_5_gt));  // open: eq, lt
  Comparator #(.width(2), .mode("unsigned")) comparator_6 (
    .a(\当前中断 ), .b(2'b10), .gt(comparator_6_gt));  // open: eq, lt
  not not_3 (not_3_out, halt);
  Multiplexer #(.width(32), .enable("false")) multiplexer_5 (
    .in0(multiplexer_10_out), .in1(breakaddr), .out(multiplexer_5_out), .sel(break2));
  Multiplexer #(.width(32), .enable("false")) multiplexer_6 (
    .in0(multiplexer_15_out), .in1(adder_1_out), .out(multiplexer_6_out), .sel(jal));
  Multiplexer #(.width(5), .enable("false")) multiplexer_7 (
    .in0(_20_16), .in1(5'b00100), .out(multiplexer_7_out), .sel(Syscall));
  Multiplexer #(.width(5), .enable("false")) multiplexer_8 (
    .in0(multiplexer_3_out), .in1({5{1'b1}}), .out(multiplexer_8_out), .sel(jal));
  Comparator #(.width(2), .mode("unsigned")) comparator_7 (.a(EXTOP), .b(2'b10), .eq(S));  // open: gt, lt
  or or_14 (or_14_out, \break , mtc0);
  Multiplexer #(.width(32), .enable("false")) multiplexer_9 (
    .in0(pc), .in1(DM), .out(multiplexer_9_out), .sel(\EPC出栈 ));
  not not_4 (not_4_out, _3break2);
  not not_5 (not_5_out, IR2_S);
  not not_6 (not_6_out, IR3_S);
  Comparator #(.width(2), .mode("unsigned")) comparator_8 (
    .a(\当前中断 ), .b(2'b00), .eq(comparator_8_eq));  // open: gt, lt
  not not_7 (not_7_out, IR3_S);
  not not_8 (not_8_out, comparator_5_gt);
  not not_9 (not_9_out, comparator_6_gt);
  Counter #(.width(16), .max('hffff)) counter_1 (
    .D(16'h1), .Q(\总周期数 ), .clk(and_14_out), .clr(RST));  // open: load, count, carry
  and and_14 (and_14_out, register_4_q, CLK);
  Register #(.width(1)) register_4 (.D(not_3_out), .Q(register_4_q), .clk(CLK), .clr(RST));  // open: en
  Multiplexer #(.width(32), .enable("false")) multiplexer_10 (
    .in0(multiplexer_13_out), .in1(RF_A), .out(multiplexer_10_out), .sel(jr));
  Multiplexer #(.select(2), .width(32), .enable("false")) multiplexer_11 (
    .in0(bit_extender_1_out), .in1(bit_extender_2_out), .in2(bit_extender_3_out), .in3({32{1'b0}}),
    .out(multiplexer_11_out), .sel(EXTOP));
  or or_15 (or_15_out, \break , \EPC出栈 );
  Multiplexer #(.select(3), .width(2), .enable("false")) multiplexer_12 (
    .in0(2'b00), .in1(2'b01), .in2(2'b10), .in3(2'b10), .in4(2'b11), .in5(2'b11), .in6(2'b11), .in7(2'b11),
    .out(\当前中断 ), .sel(IR));
  Register #(.width(3)) u_IR (.D({IR3_S, IR2_S, IR1_S}), .en(\break ), .Q(IR), .clk(CLK), .clr(or_16_out));
  or or_16 (or_16_out, eret, RST);
  and and_15 (IG1, not_4_out, IR1_S, not_5_out, not_6_out, comparator_8_eq);
  and and_16 (IG2, not_7_out, IR2_S, not_8_out);
  and and_17 (IG3, IR3_S, not_9_out);
  // RegisterFile registerfile_1: pin names not known; wires that end beside it: multiplexer_6_out, CLK, RegWrite, multiplexer_8_out, multiplexer_4_out, multiplexer_7_out, RF_A, registerfile_1_p8
  S_R_Flip_Flop s_r_ff_1 (.S(or_14_out), .clk(CLK), .R(mfc0), .Q(s_r_ff_1_q), .reset(RST));  // open: Qn, preset, en
  not not_10 (IE, s_r_ff_1_q);
  // Probe on EPC
  Register #(.width(32)) u_EPC (.D(multiplexer_9_out), .en(or_15_out), .Q(EPC), .clk(CLK), .clr(RST));
  // Probe on \当前中断 
  // Probe on IR
  not not_11 (not_11_out, eret);
  or or_17 (or_17_out, IG1, IG2, IG3);
  and and_18 (and_18_out, IG3, \break );
  Comparator #(.width(2), .mode("unsigned")) comparator_9 (
    .a(\当前中断 ), .b(2'b10), .eq(comparator_9_eq));  // open: gt, lt
  or or_18 (or_18_out, j, jal);
  Multiplexer #(.width(32), .enable("false")) multiplexer_13 (
    .in0(multiplexer_17_out), .in1({{6{1'b0}}, index[25:21], _20_16, index[15:0]}), .out(multiplexer_13_out),
    .sel(or_18_out));
  Multiplexer #(.width(32), .enable("false")) multiplexer_14 (
    .in0(registerfile_1_p8), .in1(multiplexer_11_out), .out(multiplexer_14_out), .sel(ALUsrc));
  and and_19 (\break , IE, not_11_out, or_17_out);
  and and_20 (and_20_out, and_18_out, comparator_9_eq);
  or or_19 (or_19_out, j, jal, jr);
  Multiplexer #(.width(32), .enable("false")) multiplexer_15 (
    .in0(alu_1_p5), .in1(DM), .out(multiplexer_15_out), .sel(MemToReg));
  // ALU alu_1: pin names not known; wires that end beside it: RF_A, multiplexer_14_out, ALUOP, alu_1_p4, alu_1_p5
  Multiplexer #(.width(32), .enable("false")) multiplexer_16 (
    .in0(registerfile_1_p8), .in1({{16{1'b0}}, registerfile_1_p8[15:0]}), .out(multiplexer_16_out), .sel(sh));
  Comparator #(.width(32), .mode("unsigned")) comparator_10 (
    .a(RF_A), .b(32'ha), .eq(comparator_10_eq));  // open: gt, lt
  or or_20 (w222, w2222, d_ff_5_q);
  Comparator #(.width(2), .mode("unsigned")) comparator_11 (
    .a(\当前中断 ), .b(2'b11), .eq(comparator_11_eq));  // open: gt, lt
  Counter #(.width(16), .max('hffff)) counter_2 (
    .D(16'h1), .Q(\无条件分支指令数 ), .clk(and_21_out), .clr(RST));  // open: load, count, carry
  and and_21 (and_21_out, or_19_out, not_12_out);
  not not_12 (not_12_out, CLK);
  Adder #(.width(32)) adder_2 (.a(adder_1_out), .b(multiplexer_11_out), .out(adder_2_out));  // open: cin, cout
  not not_13 (not_13_out, comparator_10_eq);
  Register #(.width(1)) register_5 (.D(\break ), .Q(break2), .clk(CLK), .clr(RST));  // open: en
  D_Flip_Flop d_ff_5 (.clk(and_20_out), .D(1'b1), .Q(d_ff_5_q), .reset(w2222));  // open: Qn, preset, en
  and and_22 (and_22_out, comparator_11_eq, \EPC出栈 );
  Multiplexer #(.width(32), .enable("false")) multiplexer_17 (
    .in0(adder_1_out), .in1(adder_2_out), .out(multiplexer_17_out), .sel(correct_b));
  or or_21 (correct_b, and_25_out, and_26_out, and_27_out);
  Multiplexer #(.width(32), .enable("false")) multiplexer_18 (
    .in0(multiplexer_16_out), .in1(EPC), .out(multiplexer_18_out), .sel(\EPC入栈 ));
  and and_23 (and_23_out, not_13_out, Syscall);
  Multiplexer #(.width(32), .enable("false")) multiplexer_19 (
    .in0(register_6_q), .in1(registerfile_1_p8), .out(multiplexer_19_out), .sel(and_23_out));
  Comparator #(.width(2), .mode("unsigned")) comparator_12 (
    .a(\当前中断 ), .b(2'b10), .lt(comparator_12_lt));  // open: gt, eq
  and and_24 (and_24_out, comparator_12_lt, \EPC出栈 );
  or or_22 (or_22_out, d_ff_5_q, w2222);
  and and_25 (and_25_out, not_15_out, blez);
  and and_26 (and_26_out, alu_1_p4, beq);
  and and_27 (and_27_out, not_16_out, bne);
  and and_28 (and_28_out, or_22_out, ~and_22_out);  // AND_Gate
  Counter #(.width(16), .max('hffff)) counter_3 (
    .D(16'h1), .Q(\有条件分支指令数 ), .clk(and_29_out), .clr(RST));  // open: load, count, carry
  and and_29 (and_29_out, or_23_out, not_14_out);
  or or_23 (or_23_out, blez, beq, bne);
  not not_14 (not_14_out, CLK);
  not not_15 (not_15_out, comparator_13_gt);
  not not_16 (not_16_out, alu_1_p4);
  RAM #(.addrWidth(16), .dataWidth(32), .bus("separate")) ram_1 (
    .addr(alu_1_p5[15:0]), .din(multiplexer_18_out), .data(DM), .str(Memwrite), .clk(CLK), .ld(MemToReg),
    .clr(RST));  // open: sel
  Register #(.width(32)) register_6 (.D(multiplexer_19_out), .en(1'b1), .Q(register_6_q), .clk(CLK), .clr(RST));
  Multiplexer #(.select(2), .width(32), .enable("false")) multiplexer_20 (
    .in0({32{1'b0}}), .in1(32'h1), .in2(32'h39), .in3(32'h71), .out(breakaddr), .sel(\当前中断 ));
  D_Flip_Flop IR1_5 (.clk(CLK), .D(and_28_out), .Q(w2222));  // open: Qn, preset, en, reset
  Comparator #(.width(32), .mode("unsigned")) comparator_13 (
    .a(RF_A), .b({32{1'b0}}), .gt(comparator_13_gt));  // open: eq, lt
  Multiplexer #(.width(32), .enable("false")) multiplexer_21 (
    .in0(register_6_q), .in1(multiplexer_19_out), .out(SyscallOut), .sel(and_23_out));
  S_R_Flip_Flop s_r_ff_2 (.S(w222), .clk(CLK), .R(and_24_out), .Q(_3break2), .reset(RST));  // open: Qn, preset, en
  Counter #(.width(16), .max('hffff)) counter_4 (
    .D(16'h1), .Q(\有条件分支成功跳转 ), .clk(and_30_out), .clr(RST));  // open: load, count, carry
  and and_30 (and_30_out, correct_b, not_17_out);
  not not_17 (not_17_out, CLK);
  and and_31 (\EPC入栈 , Memwrite, comparator_14_eq);
  Comparator #(.width(5), .mode("unsigned")) comparator_14 (
    .a(_20_16), .b(5'b11110), .eq(comparator_14_eq));  // open: gt, lt
  and and_32 (\EPC出栈 , MemToReg, comparator_15_eq);
  Comparator #(.width(5), .mode("unsigned")) comparator_15 (
    .a(_20_16), .b(5'b11110), .eq(comparator_15_eq));  // open: gt, lt

  // Other names for the same wires on the sheet: index[20:16] = _20_16

  // Notes on the sheet:
  //   指令存储器
  //   中断请求按钮
  //   中断等待响应
  //   contents of rom_1 (hex, n*v repeats v):
  //   8000ca9 23bdfffc afb10000 23bdfffc afa40000 23bdfffc afa20000 23bdfffc afbe0000 40000000 20110001
  //   118f00 112020 20020022 c 118903 112020 20020022 c 118903 112020 20020022 c 118903 112020 20020022 c
  //   118903 112020 20020022 c 118903 112020 20020022 c 118903 112020 20020022 c 118903 112020 20020022 c
  //   118903 112020 20020022 40800000 8fbe0000 23bd0004 8fa20000 23bd0004 8fa40000 23bd0004 8fb10000
  //   23bd0004 40000000 42000018 23bdfffc afb10000 23bdfffc afa40000 23bdfffc afa20000 23bdfffc afbe0000
  //   40000000 20110002 118f00 112020 20020022 c 118903 112020 20020022 c 118903 112020 20020022 c 118903
  //   112020 20020022 c 118903 112020 20020022 c 118903 112020 20020022 c 118903 112020 20020022 c 118903
  //   112020 20020022 c 118903 112020 20020022 40800000 8fbe0000 23bd0004 8fa20000 23bd0004 8fa40000
  //   23bd0004 8fb10000 23bd0004 40000000 42000018 23bdfffc afb10000 23bdfffc afa40000 23bdfffc afa20000
  //   23bdfffc afbe0000 40000000 20110003 118f00 112020 20020022 c 118903 112020 20020022 c 118903 112020
  //   20020022 c 118903 112020 20020022 c 118903 112020 20020022 c 118903 112020 20020022 c 118903 112020
  //   20020022 c 118903 112020 20020022 c 118903 112020 20020022 40800000 8fbe0000 23bd0004 8fa20000
  //   23bd0004 8fa40000 23bd0004 8fb10000 23bd0004 40000000 42000018 201d2ffc 20040000 20840001 20020022 c
  //   8000cab
  //   中断请求信号
  //   数码管输出
  //   Reset 
  //   Reset 
  //   Reset 
  //   中断请求信号
  //   响应1后，中断等待信号和请求信号清0
  //   控制器
  //   Reset 
  //   有1号中断等待且当前没有中断时
  //   寄存器文件
  //   中断周期_保存断点，关中断
  //   break,mtc0关中断
  //   中断请求寄存器
  //   mfc0开中断
  //   中断服务程序执行完毕后清0
  //   哪个执行完了就清除哪一位
  //   中断周期保存断点标志
  //   保存正在执行的中断程序对应的中断请求信号
  //   中断周期写入PC标志
  //   数据存储器
  //   Reset 
  //   中断号
  //   中断服务程序地址
endmodule

module controller (
  input  [5:0] func,
  input  [5:0] op,
  input  [4:0] _25_21,
  output RegDst,
  output ALUsrc,
  output RegWrite,
  output MemToReg,
  output MemWrite,
  output [1:0] EXTOP,
  output blez,
  output beq,
  output bne,
  output j,
  output jal,
  output jr,
  output Syscall,
  output [3:0] ALUOP,
  output sh,
  output eret,
  output mfc0,
  output mtc0
);

  wire add, add_out, addi_out, addiu_out, addu_out, \and , and_out, andi_out, \nor , not_1_out, not_2_out,
       not_3_out, not_4_out, not_5_out, not_6_out, not_7_out, not_8_out, not_9_out, not_10_out, not_11_out,
       not_12_out, not_13_out, not_14_out, not_15_out, not_16_out, not_17_out, not_18_out, not_19_out,
       not_20_out, not_21_out, not_22_out, not_23_out, not_24_out, not_25_out, not_26_out, not_27_out,
       not_28_out, \or , or_out, sll, slt, slt_out, slti_out, sltiu_out, sltu, sltu_out, sra, srl, sub,
       sw_out, \xor ;

  not not_1 (not_1_out, func[5]);
  not not_2 (not_2_out, func[3]);
  not not_3 (not_3_out, func[4]);
  not not_4 (not_4_out, _25_21[3]);
  not not_5 (not_5_out, _25_21[4]);
  not not_6 (not_6_out, func[2]);
  not not_7 (not_7_out, func[1]);
  not not_8 (not_8_out, _25_21[2]);
  not not_9 (not_9_out, _25_21[1]);
  not not_10 (not_10_out, func[0]);
  not not_11 (not_11_out, _25_21[0]);
  not not_12 (not_12_out, op[4]);
  not not_13 (not_13_out, op[5]);
  not not_14 (not_14_out, op[3]);
  not not_15 (not_15_out, op[2]);
  not not_16 (not_16_out, op[0]);
  not not_17 (not_17_out, op[1]);
  and u_add (add_out, not_13_out, not_12_out, not_14_out, not_15_out, not_17_out, not_16_out, func[5], not_3_out, not_2_out, not_6_out, not_7_out, not_10_out);
  and addi (addi_out, not_13_out, not_12_out, op[3], not_15_out, not_17_out, not_16_out);
  and addiu (addiu_out, not_13_out, not_12_out, op[3], not_15_out, not_17_out, op[0]);
  and addu (addu_out, not_13_out, not_12_out, not_14_out, not_15_out, not_17_out, not_16_out, func[5], not_3_out, not_2_out, not_6_out, not_7_out, func[0]);
  and u_and (and_out, not_13_out, not_12_out, not_14_out, not_15_out, not_17_out, not_16_out, func[5], not_3_out, not_2_out, func[2], not_7_out, not_10_out);
  and andi (andi_out, not_13_out, not_12_out, op[3], op[2], not_17_out, not_16_out);
  and u_sll (sll, not_13_out, not_12_out, not_14_out, not_15_out, not_17_out, not_16_out, not_1_out, not_3_out, not_2_out, not_6_out, not_7_out, not_10_out);
  and u_sra (sra, not_13_out, not_12_out, not_14_out, not_15_out, not_17_out, not_16_out, not_1_out, not_3_out, not_2_out, not_6_out, func[1], func[0]);
  and u_srl (srl, not_13_out, not_12_out, not_14_out, not_15_out, not_17_out, not_16_out, not_1_out, not_3_out, not_2_out, not_6_out, func[1], not_10_out);
  and u_sub (sub, not_13_out, not_12_out, not_14_out, not_15_out, not_17_out, not_16_out, func[5], not_3_out, not_2_out, not_6_out, func[1], not_10_out);
  and u_or (or_out, not_13_out, not_12_out, not_14_out, not_15_out, not_17_out, not_16_out, func[5], not_3_out, not_2_out, func[2], not_7_out, func[0]);
  and ori (EXTOP[0], not_13_out, not_12_out, op[3], op[2], not_17_out, op[0]);
  and u_nor (\nor , not_13_out, not_12_out, not_14_out, not_15_out, not_17_out, not_16_out, func[5], not_3_out, not_2_out, func[2], func[1], func[0]);
  and lw (MemToReg, op[5], not_12_out, not_14_out, not_15_out, op[1], op[0]);
  and sw (sw_out, op[5], not_12_out, op[3], not_15_out, op[1], op[0]);
  and u_beq (beq, not_13_out, not_12_out, not_14_out, op[2], not_17_out, not_16_out);
  and u_bne (bne, not_13_out, not_12_out, not_14_out, op[2], not_17_out, op[0]);
  and u_slt (slt_out, not_13_out, not_12_out, not_14_out, not_15_out, not_17_out, not_16_out, func[5], not_3_out, func[3], not_6_out, func[1], not_10_out);
  and slti (slti_out, not_13_out, not_12_out, op[3], not_15_out, op[1], not_16_out);
  and u_sltu (sltu_out, not_13_out, not_12_out, not_14_out, not_15_out, not_17_out, not_16_out, func[5], not_3_out, func[3], not_6_out, func[1], func[0]);
  and u_j (j, not_13_out, not_12_out, not_14_out, not_15_out, op[1], not_16_out);
  and u_jal (jal, not_13_out, not_12_out, not_14_out, not_15_out, op[1], op[0]);
  and u_jr (jr, not_13_out, not_12_out, not_14_out, not_15_out, not_17_out, not_16_out, not_1_out, not_3_out, func[3], not_6_out, not_7_out, not_10_out);
  and u_syscall (Syscall, not_13_out, not_12_out, not_14_out, not_15_out, not_17_out, not_16_out, not_1_out, not_3_out, func[3], func[2], not_7_out, not_10_out);
  and u_xor (\xor , not_13_out, not_12_out, not_14_out, not_15_out, not_17_out, not_16_out, func[5], not_3_out, not_2_out, func[2], func[1], not_10_out);
  and sltiu (sltiu_out, not_13_out, not_12_out, op[3], not_15_out, op[1], op[0]);
  and u_sh (sh, op[5], not_12_out, op[3], not_15_out, not_17_out, op[0]);
  and u_blez (blez, not_13_out, not_12_out, not_14_out, op[2], op[1], not_16_out);
  and u_eret (eret, not_13_out, op[4], not_14_out, not_15_out, not_17_out, not_16_out, not_1_out, func[4], func[3], not_6_out, not_7_out, not_10_out);
  and u_mfc0 (mfc0, not_13_out, op[4], not_14_out, not_15_out, not_17_out, not_16_out, not_5_out, not_4_out, not_8_out, not_9_out, not_11_out);
  and u_mtc0 (mtc0, not_13_out, op[4], not_14_out, not_15_out, not_17_out, not_16_out, not_5_out, not_4_out, _25_21[2], not_9_out, not_11_out);
  or or_2 (RegDst, add_out, addu_out, and_out, sll, sra, srl, sub, or_out, \nor , slt_out, sltu_out, \xor );
  or or_3 (ALUsrc, addi_out, addiu_out, andi_out, sll, sra, srl, EXTOP[0], MemToReg, sw_out, slti_out, sltiu_out, sh);
  or or_4 (RegWrite, add_out, addi_out, addiu_out, addu_out, and_out, andi_out, sll, sra, srl, sub, or_out, EXTOP[0], \nor , MemToReg, slt_out, slti_out, sltu_out, jal, \xor , sltiu_out);
  or or_5 (MemWrite, sw_out, sh);
  or or_6 (EXTOP[1], sll, sra, srl);
  or and_2 (\and , and_out, andi_out);
  or or_7 (\or , or_out, EXTOP[0]);
  or slt_2 (slt, slt_out, slti_out);
  or ALUOP3 (ALUOP[3], \or , \xor , \nor , slt, sltu);
  or ALUOP2 (ALUOP[2], add, sub, \and , sltu);
  or ALUOP1 (ALUOP[1], srl, sub, \and , \nor , slt);
  or ALUOP0 (ALUOP[0], sra, add, \and , \xor , slt);
  or sltu_2 (sltu, sltu_out, sltiu_out);
  not not_18 (not_18_out, sra);
  not not_19 (not_19_out, sll);
  or add_2 (add, add_out, addi_out, addiu_out, addu_out, MemToReg, sw_out, sh);
  not not_20 (not_20_out, srl);
  not not_21 (not_21_out, add);
  not not_22 (not_22_out, sub);
  not not_23 (not_23_out, \and );
  not not_24 (not_24_out, \or );
  not not_25 (not_25_out, \xor );
  not not_26 (not_26_out, slt);
  not not_27 (not_27_out, \nor );
  not not_28 (not_28_out, sltu);
endmodule
