// Logisim project mipsalu.circ as structural Verilog: 1 circuit, main circuit main
module main (
  input  [31:0] in_1,
  input  [31:0] in_2,
  input  [3:0] in_3,
  output [31:0] out_4
);

  wire mips_alu_1_p4;

  // Probe on in_1
  // Probe on in_2
  // Mips_ALU mips_alu_1: pin names not known; wires that end beside it: in_1, in_2, in_3, mips_alu_1_p4, mips_alu_1_p4, out_4
  // Probe on out_4
endmodule
