// Logisim project logisim-常见故障.circ as structural Verilog: 6 circuits, main circuit 震荡电路
module \震荡电路  (
  input  in_1,
  output out_2
);

  nand nand_1 (out_2, in_1, out_2);

  // Notes on the sheet:
  //   尝试修改输入引脚的电平,输入输出存在反馈，导致电路状态不稳定
  //   如出现类似情况，尝试去掉部分回路连接直至故障消除
  //   华中科技大学计算机学院 计算机组成原理
endmodule

module \信号冲突  (
  input  in_1,
  input  in_2,
  output out_3
);


  assign in_2 = in_1;
  assign out_3 = in_1;

  // Notes on the sheet:
  //   输入相同时无问题，不同时出错，红色显示
  //   华中科技大学计算机学院 计算机组成原理
endmodule

module \不同颜色信号线  (
  input  \引脚类型不对 ,
  input  [1:0] in_2,
  input  in_3
);

  wire undriven;
  wire [1:0] nand_2_out, undriven_3;
  wire [1:1] undriven_2;

  nand nand_1 (\引脚类型不对 , 1'b1, 1'b0, undriven, 1'b0);
  assign nand_2_out = ~(in_2 & undriven_3 & {undriven_2[1], in_3});  // NAND_Gate nand_2, 2 bits wide
  // Pins of 1 and 2 bits meet at {undriven_2[1], in_3}

  // Notes on the sheet:
  //   深绿色表示高电平
  //   蓝色表示未知状态
  //   灰色表示飞线
  //   亮绿色表示高电平
  //   红色表示信号冲突
  //   黑色表示多位总线
  //   橙色表示位宽不匹配
  //   华中科技大学计算机学院 计算机组成原理
endmodule

module \分线器使用  (
  input  [7:0] in_1
);


  // Notes on the sheet:
  //   分线器使用方法
  //   8分3，两个3位，一个2位
  //   分线器不分输入输出，可反向使用进行线缆汇总
  //   华中科技大学计算机学院 计算机组成原理
  //   8分二，高位在下
  //   8分二，高位在上
  //   只分部分位，位宽不对称
  //   只分1位，如取符号位
  //   8分8
endmodule

module \毛刺  (
);

  wire and_1_out, clock_1_out, not_1_out;

  Clock clock_1 (.out(clock_1_out));
  Counter counter_1 (.clk(clock_1_out));  // open: load, D, count, Q, carry, clr
  not not_1 (not_1_out, clock_1_out);
  and and_1 (and_1_out, not_1_out, clock_1_out);
  Counter counter_2 (.clk(and_1_out));  // open: load, D, count, Q, carry, clr

  // Notes on the sheet:
  //   此计数器不可能计数，但试试看？为什么？
endmodule

module MUX (
  input  in_1,
  input  in_2,
  output out_3
);

  wire not_1_out;

  Multiplexer #(.enable("false")) multiplexer_1 (.in0(in_1), .in1(in_2), .out(out_3), .sel(not_1_out));
  not not_1 (not_1_out, out_3);

  // Notes on the sheet:
  //   类似震荡
endmodule
